// Logisim project CPU Gate Problem.circ as structural Verilog: 24 circuits, main circuit main
module main (
);

  wire _1_out, _2_out, button_press_spike_generator_1_in0, button_press_spike_generator_1_in1,
       button_press_spike_generator_1_in1_2, button_press_spike_generator_1_in1_3,
       button_press_spike_generator_1_in1_4, button_press_spike_generator_1_in1_5,
       button_press_spike_generator_1_in1_6, button_press_spike_generator_1_in1_7, Cancel_out, clock_1_out,
       processor_1_o0, processor_1_o1, processor_1_o2, processor_1_o3;
  wire [7:0] processor_1_out_18, rom_1_data;

  ROM rom_1 (.addr(processor_1_out_18), .data(rom_1_data));  // open: sel
  Processor processor_1 (
    .out_18(processor_1_out_18), .ROM0(rom_1_data[0]), .ROM1(rom_1_data[1]), .ROM2(rom_1_data[2]),
    .ROM3(rom_1_data[3]), .ROM4(rom_1_data[4]), .ROM5(rom_1_data[5]), .ROM6(rom_1_data[6]),
    .ROM7(rom_1_data[7]), .CK(clock_1_out), .O0(processor_1_o0), .O1(processor_1_o1), .O2(processor_1_o2),
    .O3(processor_1_o3), .I0(button_press_spike_generator_1_in0), .I1(button_press_spike_generator_1_in1),
    .I2(button_press_spike_generator_1_in1_2), .I3(button_press_spike_generator_1_in1_3),
    .I4(button_press_spike_generator_1_in1_4), .I5(button_press_spike_generator_1_in1_5),
    .I6(button_press_spike_generator_1_in1_6), .I7(button_press_spike_generator_1_in1_7));  // open: O4, O5, O6, O7
  BUTTON_PRESS_SPIKE_GENERATOR button_press_spike_generator_1 (
    .CK(clock_1_out), .BTN0(_1_out), .BTN1(_2_out), .BTN1_2(Cancel_out), .BTN1_3(1'b0), .BTN1_4(1'b0),
    .BTN1_5(1'b0), .BTN1_6(1'b0), .BTN1_7(1'b0), .IN0(button_press_spike_generator_1_in0),
    .IN1(button_press_spike_generator_1_in1), .IN1_2(button_press_spike_generator_1_in1_2),
    .IN1_3(button_press_spike_generator_1_in1_3), .IN1_4(button_press_spike_generator_1_in1_4),
    .IN1_5(button_press_spike_generator_1_in1_5), .IN1_6(button_press_spike_generator_1_in1_6),
    .IN1_7(button_press_spike_generator_1_in1_7));
  Clock clock_1 (.out(clock_1_out));
  Button _1 (.out(_1_out));
  Button _2 (.out(_2_out));
  Button Cancel (.out(Cancel_out));
  LED OPEN (.in(processor_1_o0));
  LED Return__1 (.in(processor_1_o1));
  LED Return__2 (.in(processor_1_o2));
  LED Return__3 (.in(processor_1_o3));

  // Notes on the sheet:
  //   contents of rom_1 (hex, n*v repeats v):
  //   e3 5 7 0 34 19 5 7 12 3 15 4 2 e4 f4 5 7 4a 33 29 5 7 1f 3 25 4 2 e4 f4 5 7 4a 2 e4 f4 3 6 fd 8 31
  //   15 8 37 15 8 3f 15 8 0 82 f4 2 4 5 7 0 42 f4 2 4 5 7 0 22 f4 2 4 5 7 0 2 5 7 0 3 6 fb 8 55 15 8 5c
  //   f5 8 0 12 f4 4 2 5 7 0 12 f4 2 4 5 7
endmodule

module Working_Register (
  input  X0,
  input  X1,
  input  X2,
  input  X3,
  input  X4,
  input  X5,
  input  X6,
  input  X7,
  input  CK,
  output X0_2,
  output X1_2,
  output X2_2,
  output X3_2,
  output X4_2,
  output X5_2,
  output X6_2,
  output X7_2
);

  D_Flip_Flop #(.trigger("falling")) d_ff_1 (.clk(CK), .D(X0), .Q(X0_2));  // open: Qn, preset, en, reset
  D_Flip_Flop #(.trigger("falling")) d_ff_2 (.clk(CK), .D(X1), .Q(X1_2));  // open: Qn, preset, en, reset
  D_Flip_Flop #(.trigger("falling")) d_ff_3 (.clk(CK), .D(X2), .Q(X2_2));  // open: Qn, preset, en, reset
  D_Flip_Flop #(.trigger("falling")) d_ff_4 (.clk(CK), .D(X3), .Q(X3_2));  // open: Qn, preset, en, reset
  D_Flip_Flop #(.trigger("falling")) d_ff_5 (.clk(CK), .D(X4), .Q(X4_2));  // open: Qn, preset, en, reset
  D_Flip_Flop #(.trigger("falling")) d_ff_6 (.clk(CK), .D(X5), .Q(X5_2));  // open: Qn, preset, en, reset
  D_Flip_Flop #(.trigger("falling")) d_ff_7 (.clk(CK), .D(X6), .Q(X6_2));  // open: Qn, preset, en, reset
  D_Flip_Flop #(.trigger("falling")) d_ff_8 (.clk(CK), .D(X7), .Q(X7_2));  // open: Qn, preset, en, reset
endmodule

module RAM (
  input  A0,
  input  A1,
  input  A2,
  input  A3,
  input  RD,
  input  WD,
  input  S0,
  input  S1,
  input  S2,
  input  S3,
  input  S4,
  input  S5,
  input  S6,
  input  S7,
  input  IN0,
  input  IN1,
  input  IN2,
  input  IN3,
  input  IN4,
  input  IN5,
  input  IN6,
  input  IN7,
  output S0_2,
  output S1_2,
  output S2_2,
  output S3_2,
  output S4_2,
  output S5_2,
  output S6_2,
  output S7_2,
  output OUT0,
  output OUT1,
  output OUT2,
  output OUT3,
  output OUT4,
  output OUT5,
  output OUT6,
  output OUT7
);

  wire and_1_out, n1_byte_ram_1_s0_2, n1_byte_ram_1_s1_2, n1_byte_ram_1_s2_2, n1_byte_ram_1_s3_2,
       n1_byte_ram_1_s4_2, n1_byte_ram_1_s5_2, n1_byte_ram_1_s6_2, n1_byte_ram_1_s7_2, n1_byte_ram_2_s0_2,
       n1_byte_ram_2_s1_2, n1_byte_ram_2_s2_2, n1_byte_ram_2_s3_2, n1_byte_ram_2_s4_2, n1_byte_ram_2_s5_2,
       n1_byte_ram_2_s6_2, n1_byte_ram_2_s7_2, n1_byte_ram_3_s0_2, n1_byte_ram_3_s1_2, n1_byte_ram_3_s2_2,
       n1_byte_ram_3_s3_2, n1_byte_ram_3_s4_2, n1_byte_ram_3_s5_2, n1_byte_ram_3_s6_2, n1_byte_ram_3_s7_2,
       n1_byte_ram_4_s0_2, n1_byte_ram_4_s1_2, n1_byte_ram_4_s2_2, n1_byte_ram_4_s3_2, n1_byte_ram_4_s4_2,
       n1_byte_ram_4_s5_2, n1_byte_ram_4_s6_2, n1_byte_ram_4_s7_2, n1_byte_ram_5_s0_2, n1_byte_ram_5_s1_2,
       n1_byte_ram_5_s2_2, n1_byte_ram_5_s3_2, n1_byte_ram_5_s4_2, n1_byte_ram_5_s5_2, n1_byte_ram_5_s6_2,
       n1_byte_ram_5_s7_2, n1_byte_ram_6_s0_2, n1_byte_ram_6_s1_2, n1_byte_ram_6_s2_2, n1_byte_ram_6_s3_2,
       n1_byte_ram_6_s4_2, n1_byte_ram_6_s5_2, n1_byte_ram_6_s6_2, n1_byte_ram_6_s7_2, n1_byte_ram_7_s0_2,
       n1_byte_ram_7_s1_2, n1_byte_ram_7_s2_2, n1_byte_ram_7_s3_2, n1_byte_ram_7_s4_2, n1_byte_ram_7_s5_2,
       n1_byte_ram_7_s6_2, n1_byte_ram_7_s7_2, n1_byte_ram_8_s0_2, n1_byte_ram_8_s1_2, n1_byte_ram_8_s2_2,
       n1_byte_ram_8_s3_2, n1_byte_ram_8_s4_2, n1_byte_ram_8_s5_2, n1_byte_ram_8_s6_2, n1_byte_ram_8_s7_2,
       n1_byte_ram_9_s0_2, n1_byte_ram_9_s1_2, n1_byte_ram_9_s2_2, n1_byte_ram_9_s3_2, n1_byte_ram_9_s4_2,
       n1_byte_ram_9_s5_2, n1_byte_ram_9_s6_2, n1_byte_ram_9_s7_2, n1_byte_ram_10_s0_2, n1_byte_ram_10_s1_2,
       n1_byte_ram_10_s2_2, n1_byte_ram_10_s3_2, n1_byte_ram_10_s4_2, n1_byte_ram_10_s5_2,
       n1_byte_ram_10_s6_2, n1_byte_ram_10_s7_2, n1_byte_ram_11_s0_2, n1_byte_ram_11_s1_2,
       n1_byte_ram_11_s2_2, n1_byte_ram_11_s3_2, n1_byte_ram_11_s4_2, n1_byte_ram_11_s5_2,
       n1_byte_ram_11_s6_2, n1_byte_ram_11_s7_2, n1_byte_ram_12_s0_2, n1_byte_ram_12_s1_2,
       n1_byte_ram_12_s2_2, n1_byte_ram_12_s3_2, n1_byte_ram_12_s4_2, n1_byte_ram_12_s5_2,
       n1_byte_ram_12_s6_2, n1_byte_ram_12_s7_2, n1_byte_ram_13_s0_2, n1_byte_ram_13_s1_2,
       n1_byte_ram_13_s2_2, n1_byte_ram_13_s3_2, n1_byte_ram_13_s4_2, n1_byte_ram_13_s5_2,
       n1_byte_ram_13_s6_2, n1_byte_ram_13_s7_2, n1_byte_ram_14_s0_2, n1_byte_ram_14_s1_2,
       n1_byte_ram_14_s2_2, n1_byte_ram_14_s3_2, n1_byte_ram_14_s4_2, n1_byte_ram_14_s5_2,
       n1_byte_ram_14_s6_2, n1_byte_ram_14_s7_2, n1_byte_ram_15_s0_2, n1_byte_ram_15_s1_2,
       n1_byte_ram_15_s2_2, n1_byte_ram_15_s3_2, n1_byte_ram_15_s4_2, n1_byte_ram_15_s5_2,
       n1_byte_ram_15_s6_2, n1_byte_ram_15_s7_2, n8_bit_or_1_s0, n8_bit_or_1_s1, n8_bit_or_1_s2,
       n8_bit_or_1_s3, n8_bit_or_1_s4, n8_bit_or_1_s5, n8_bit_or_1_s6, n8_bit_or_1_s7, n8_bit_or_2_s0,
       n8_bit_or_2_s1, n8_bit_or_2_s2, n8_bit_or_2_s3, n8_bit_or_2_s4, n8_bit_or_2_s5, n8_bit_or_2_s6,
       n8_bit_or_2_s7, n8_bit_or_3_s0, n8_bit_or_3_s1, n8_bit_or_3_s2, n8_bit_or_3_s3, n8_bit_or_3_s4,
       n8_bit_or_3_s5, n8_bit_or_3_s6, n8_bit_or_3_s7, n8_bit_or_4_s0, n8_bit_or_4_s1, n8_bit_or_4_s2,
       n8_bit_or_4_s3, n8_bit_or_4_s4, n8_bit_or_4_s5, n8_bit_or_4_s6, n8_bit_or_4_s7, n8_bit_or_5_s0,
       n8_bit_or_5_s1, n8_bit_or_5_s2, n8_bit_or_5_s3, n8_bit_or_5_s4, n8_bit_or_5_s5, n8_bit_or_5_s6,
       n8_bit_or_5_s7, n8_bit_or_6_s0, n8_bit_or_6_s1, n8_bit_or_6_s2, n8_bit_or_6_s3, n8_bit_or_6_s4,
       n8_bit_or_6_s5, n8_bit_or_6_s6, n8_bit_or_6_s7, n8_bit_or_7_s0, n8_bit_or_7_s1, n8_bit_or_7_s2,
       n8_bit_or_7_s3, n8_bit_or_7_s4, n8_bit_or_7_s5, n8_bit_or_7_s6, n8_bit_or_7_s7, n8_bit_or_8_s0,
       n8_bit_or_8_s1, n8_bit_or_8_s2, n8_bit_or_8_s3, n8_bit_or_8_s4, n8_bit_or_8_s5, n8_bit_or_8_s6,
       n8_bit_or_8_s7, n8_bit_or_9_s0, n8_bit_or_9_s1, n8_bit_or_9_s2, n8_bit_or_9_s3, n8_bit_or_9_s4,
       n8_bit_or_9_s5, n8_bit_or_9_s6, n8_bit_or_9_s7, n8_bit_or_10_s0, n8_bit_or_10_s1, n8_bit_or_10_s2,
       n8_bit_or_10_s3, n8_bit_or_10_s4, n8_bit_or_10_s5, n8_bit_or_10_s6, n8_bit_or_10_s7, n8_bit_or_11_s0,
       n8_bit_or_11_s1, n8_bit_or_11_s2, n8_bit_or_11_s3, n8_bit_or_11_s4, n8_bit_or_11_s5, n8_bit_or_11_s6,
       n8_bit_or_11_s7, n8_bit_or_12_s0, n8_bit_or_12_s1, n8_bit_or_12_s2, n8_bit_or_12_s3, n8_bit_or_12_s4,
       n8_bit_or_12_s5, n8_bit_or_12_s6, n8_bit_or_12_s7, n8_bit_or_13_s0, n8_bit_or_13_s1, n8_bit_or_13_s2,
       n8_bit_or_13_s3, n8_bit_or_13_s4, n8_bit_or_13_s5, n8_bit_or_13_s6, n8_bit_or_13_s7, n8_bit_or_14_s0,
       n8_bit_or_14_s1, n8_bit_or_14_s2, n8_bit_or_14_s3, n8_bit_or_14_s4, n8_bit_or_14_s5, n8_bit_or_14_s6,
       n8_bit_or_14_s7, not_1_out, not_2_out, not_3_out, not_4_out, not_5_out, not_6_out, not_7_out,
       not_8_out, not_9_out, not_10_out, not_11_out, not_12_out, not_13_out, not_14_out, not_15_out,
       not_16_out, not_17_out, not_18_out, not_19_out, not_20_out, not_21_out, not_22_out, not_23_out,
       not_24_out, not_25_out, not_26_out, not_27_out, not_28_out, not_29_out, not_30_out, not_31_out,
       not_32_out, or_1_out, or_2_out, or_3_out, or_4_out, or_5_out, or_6_out, or_7_out, or_8_out, or_9_out,
       ram_chip_select_logic_1__0x00, ram_chip_select_logic_1__0x0a, ram_chip_select_logic_1__0x0b,
       ram_chip_select_logic_1__0x0c, ram_chip_select_logic_1__0x0d, ram_chip_select_logic_1__0x0e,
       ram_chip_select_logic_1__0x0f, ram_chip_select_logic_1__0x01, ram_chip_select_logic_1__0x02,
       ram_chip_select_logic_1__0x03, ram_chip_select_logic_1__0x04, ram_chip_select_logic_1__0x05,
       ram_chip_select_logic_1__0x06, ram_chip_select_logic_1__0x07, ram_chip_select_logic_1__0x08,
       ram_chip_select_logic_1__0x09;

  RAM_chip_select_LOGIC ram_chip_select_logic_1 (
    .A0(A0), .A1(A1), .A2(A2), .A3(A3), ._0x00(ram_chip_select_logic_1__0x00),
    ._0x01(ram_chip_select_logic_1__0x01), ._0x02(ram_chip_select_logic_1__0x02),
    ._0x03(ram_chip_select_logic_1__0x03), ._0x04(ram_chip_select_logic_1__0x04),
    ._0x05(ram_chip_select_logic_1__0x05), ._0x06(ram_chip_select_logic_1__0x06),
    ._0x07(ram_chip_select_logic_1__0x07), ._0x08(ram_chip_select_logic_1__0x08),
    ._0x09(ram_chip_select_logic_1__0x09), ._0x0A(ram_chip_select_logic_1__0x0a),
    ._0x0B(ram_chip_select_logic_1__0x0b), ._0x0C(ram_chip_select_logic_1__0x0c),
    ._0x0D(ram_chip_select_logic_1__0x0d), ._0x0E(ram_chip_select_logic_1__0x0e),
    ._0x0F(ram_chip_select_logic_1__0x0f));
  or or_1 (or_1_out, or_3_out, or_2_out);
  or or_2 (or_2_out, or_5_out, or_6_out);
  or or_3 (or_3_out, or_7_out, or_8_out);
  or or_4 (or_4_out, ram_chip_select_logic_1__0x0e, or_1_out);
  and and_1 (and_1_out, WD, ram_chip_select_logic_1__0x0f);
  or or_5 (or_5_out, IN0, IN1);
  or or_6 (or_6_out, IN2, IN3);
  or or_7 (or_7_out, IN4, IN5);
  or or_8 (or_8_out, IN6, IN7);
  or or_9 (or_9_out, WD, or_1_out);
  not not_1 (not_1_out, not_8_out);
  not not_2 (not_2_out, not_9_out);
  not not_3 (not_3_out, not_12_out);
  not not_4 (not_4_out, not_13_out);
  not not_5 (not_5_out, not_11_out);
  not not_6 (not_6_out, not_10_out);
  not not_7 (not_7_out, not_14_out);
  not not_8 (not_8_out, not_15_out);
  not not_9 (not_9_out, not_21_out);
  not not_10 (not_10_out, not_18_out);
  not not_11 (not_11_out, not_17_out);
  not not_12 (not_12_out, not_16_out);
  not not_13 (not_13_out, not_20_out);
  not not_14 (not_14_out, not_19_out);
  not not_15 (not_15_out, not_24_out);
  not not_16 (not_16_out, not_27_out);
  not not_17 (not_17_out, not_26_out);
  not not_18 (not_18_out, not_23_out);
  not not_19 (not_19_out, not_25_out);
  not not_20 (not_20_out, not_22_out);
  not not_21 (not_21_out, not_28_out);
  not not_22 (not_22_out, n8_bit_or_1_s0);
  not not_23 (not_23_out, n8_bit_or_1_s3);
  not not_24 (not_24_out, n8_bit_or_1_s6);
  not not_25 (not_25_out, n8_bit_or_1_s1);
  not not_26 (not_26_out, n8_bit_or_1_s2);
  not not_27 (not_27_out, n8_bit_or_1_s4);
  not not_28 (not_28_out, n8_bit_or_1_s5);
  _8_Bit_OR u_8_bit_or_1 (
    .A0(IN0), .B0(S0), .A1(IN1), .B1(S1), .A2(IN2), .B2(S2), .A3(IN3), .B3(S3), .A4(IN4), .B4(S4), .A5(IN5),
    .B5(S5), .A6(IN6), .B6(S6), .A7(IN7), .B7(S7), .S0(n8_bit_or_1_s0), .S1(n8_bit_or_1_s1),
    .S2(n8_bit_or_1_s2), .S3(n8_bit_or_1_s3), .S4(n8_bit_or_1_s4), .S5(n8_bit_or_1_s5), .S6(n8_bit_or_1_s6),
    .S7(n8_bit_or_1_s7));
  not not_29 (not_29_out, not_30_out);
  not not_30 (not_30_out, not_31_out);
  not not_31 (not_31_out, not_32_out);
  not not_32 (not_32_out, n8_bit_or_1_s7);
  _1_Byte_ram u_1_byte_ram_1 (
    .AD(ram_chip_select_logic_1__0x00), .RD(RD), .WD(WD), .S0(S0), .S1(S1), .S2(S2), .S3(S3), .S4(S4),
    .S5(S5), .S6(S6), .S7(S7), .S0_2(n1_byte_ram_1_s0_2), .S1_2(n1_byte_ram_1_s1_2),
    .S2_2(n1_byte_ram_1_s2_2), .S3_2(n1_byte_ram_1_s3_2), .S4_2(n1_byte_ram_1_s4_2),
    .S5_2(n1_byte_ram_1_s5_2), .S6_2(n1_byte_ram_1_s6_2), .S7_2(n1_byte_ram_1_s7_2));
  _1_Byte_ram u_1_byte_ram_2 (
    .AD(ram_chip_select_logic_1__0x01), .RD(RD), .WD(WD), .S0(S0), .S1(S1), .S2(S2), .S3(S3), .S4(S4),
    .S5(S5), .S6(S6), .S7(S7), .S0_2(n1_byte_ram_2_s0_2), .S1_2(n1_byte_ram_2_s1_2),
    .S2_2(n1_byte_ram_2_s2_2), .S3_2(n1_byte_ram_2_s3_2), .S4_2(n1_byte_ram_2_s4_2),
    .S5_2(n1_byte_ram_2_s5_2), .S6_2(n1_byte_ram_2_s6_2), .S7_2(n1_byte_ram_2_s7_2));
  _1_Byte_ram u_1_byte_ram_3 (
    .AD(ram_chip_select_logic_1__0x02), .RD(RD), .WD(WD), .S0(S0), .S1(S1), .S2(S2), .S3(S3), .S4(S4),
    .S5(S5), .S6(S6), .S7(S7), .S0_2(n1_byte_ram_3_s0_2), .S1_2(n1_byte_ram_3_s1_2),
    .S2_2(n1_byte_ram_3_s2_2), .S3_2(n1_byte_ram_3_s3_2), .S4_2(n1_byte_ram_3_s4_2),
    .S5_2(n1_byte_ram_3_s5_2), .S6_2(n1_byte_ram_3_s6_2), .S7_2(n1_byte_ram_3_s7_2));
  _1_Byte_ram u_1_byte_ram_4 (
    .AD(ram_chip_select_logic_1__0x03), .RD(RD), .WD(WD), .S0(S0), .S1(S1), .S2(S2), .S3(S3), .S4(S4),
    .S5(S5), .S6(S6), .S7(S7), .S0_2(n1_byte_ram_4_s0_2), .S1_2(n1_byte_ram_4_s1_2),
    .S2_2(n1_byte_ram_4_s2_2), .S3_2(n1_byte_ram_4_s3_2), .S4_2(n1_byte_ram_4_s4_2),
    .S5_2(n1_byte_ram_4_s5_2), .S6_2(n1_byte_ram_4_s6_2), .S7_2(n1_byte_ram_4_s7_2));
  _1_Byte_ram u_1_byte_ram_5 (
    .AD(ram_chip_select_logic_1__0x04), .RD(RD), .WD(WD), .S0(S0), .S1(S1), .S2(S2), .S3(S3), .S4(S4),
    .S5(S5), .S6(S6), .S7(S7), .S0_2(n1_byte_ram_5_s0_2), .S1_2(n1_byte_ram_5_s1_2),
    .S2_2(n1_byte_ram_5_s2_2), .S3_2(n1_byte_ram_5_s3_2), .S4_2(n1_byte_ram_5_s4_2),
    .S5_2(n1_byte_ram_5_s5_2), .S6_2(n1_byte_ram_5_s6_2), .S7_2(n1_byte_ram_5_s7_2));
  _1_Byte_ram u_1_byte_ram_6 (
    .AD(ram_chip_select_logic_1__0x05), .RD(RD), .WD(WD), .S0(S0), .S1(S1), .S2(S2), .S3(S3), .S4(S4),
    .S5(S5), .S6(S6), .S7(S7), .S0_2(n1_byte_ram_6_s0_2), .S1_2(n1_byte_ram_6_s1_2),
    .S2_2(n1_byte_ram_6_s2_2), .S3_2(n1_byte_ram_6_s3_2), .S4_2(n1_byte_ram_6_s4_2),
    .S5_2(n1_byte_ram_6_s5_2), .S6_2(n1_byte_ram_6_s6_2), .S7_2(n1_byte_ram_6_s7_2));
  _1_Byte_ram u_1_byte_ram_7 (
    .AD(ram_chip_select_logic_1__0x06), .RD(RD), .WD(WD), .S0(S0), .S1(S1), .S2(S2), .S3(S3), .S4(S4),
    .S5(S5), .S6(S6), .S7(S7), .S0_2(n1_byte_ram_7_s0_2), .S1_2(n1_byte_ram_7_s1_2),
    .S2_2(n1_byte_ram_7_s2_2), .S3_2(n1_byte_ram_7_s3_2), .S4_2(n1_byte_ram_7_s4_2),
    .S5_2(n1_byte_ram_7_s5_2), .S6_2(n1_byte_ram_7_s6_2), .S7_2(n1_byte_ram_7_s7_2));
  _1_Byte_ram u_1_byte_ram_8 (
    .AD(ram_chip_select_logic_1__0x07), .RD(RD), .WD(WD), .S0(S0), .S1(S1), .S2(S2), .S3(S3), .S4(S4),
    .S5(S5), .S6(S6), .S7(S7), .S0_2(n1_byte_ram_8_s0_2), .S1_2(n1_byte_ram_8_s1_2),
    .S2_2(n1_byte_ram_8_s2_2), .S3_2(n1_byte_ram_8_s3_2), .S4_2(n1_byte_ram_8_s4_2),
    .S5_2(n1_byte_ram_8_s5_2), .S6_2(n1_byte_ram_8_s6_2), .S7_2(n1_byte_ram_8_s7_2));
  _1_Byte_ram u_1_byte_ram_9 (
    .AD(ram_chip_select_logic_1__0x08), .RD(RD), .WD(WD), .S0(S0), .S1(S1), .S2(S2), .S3(S3), .S4(S4),
    .S5(S5), .S6(S6), .S7(S7), .S0_2(n1_byte_ram_9_s0_2), .S1_2(n1_byte_ram_9_s1_2),
    .S2_2(n1_byte_ram_9_s2_2), .S3_2(n1_byte_ram_9_s3_2), .S4_2(n1_byte_ram_9_s4_2),
    .S5_2(n1_byte_ram_9_s5_2), .S6_2(n1_byte_ram_9_s6_2), .S7_2(n1_byte_ram_9_s7_2));
  _1_Byte_ram u_1_byte_ram_10 (
    .AD(ram_chip_select_logic_1__0x09), .RD(RD), .WD(WD), .S0(S0), .S1(S1), .S2(S2), .S3(S3), .S4(S4),
    .S5(S5), .S6(S6), .S7(S7), .S0_2(n1_byte_ram_10_s0_2), .S1_2(n1_byte_ram_10_s1_2),
    .S2_2(n1_byte_ram_10_s2_2), .S3_2(n1_byte_ram_10_s3_2), .S4_2(n1_byte_ram_10_s4_2),
    .S5_2(n1_byte_ram_10_s5_2), .S6_2(n1_byte_ram_10_s6_2), .S7_2(n1_byte_ram_10_s7_2));
  _1_Byte_ram u_1_byte_ram_11 (
    .AD(ram_chip_select_logic_1__0x0a), .RD(RD), .WD(WD), .S0(S0), .S1(S1), .S2(S2), .S3(S3), .S4(S4),
    .S5(S5), .S6(S6), .S7(S7), .S0_2(n1_byte_ram_11_s0_2), .S1_2(n1_byte_ram_11_s1_2),
    .S2_2(n1_byte_ram_11_s2_2), .S3_2(n1_byte_ram_11_s3_2), .S4_2(n1_byte_ram_11_s4_2),
    .S5_2(n1_byte_ram_11_s5_2), .S6_2(n1_byte_ram_11_s6_2), .S7_2(n1_byte_ram_11_s7_2));
  _1_Byte_ram u_1_byte_ram_12 (
    .AD(ram_chip_select_logic_1__0x0b), .RD(RD), .WD(WD), .S0(S0), .S1(S1), .S2(S2), .S3(S3), .S4(S4),
    .S5(S5), .S6(S6), .S7(S7), .S0_2(n1_byte_ram_12_s0_2), .S1_2(n1_byte_ram_12_s1_2),
    .S2_2(n1_byte_ram_12_s2_2), .S3_2(n1_byte_ram_12_s3_2), .S4_2(n1_byte_ram_12_s4_2),
    .S5_2(n1_byte_ram_12_s5_2), .S6_2(n1_byte_ram_12_s6_2), .S7_2(n1_byte_ram_12_s7_2));
  _1_Byte_ram u_1_byte_ram_13 (
    .AD(ram_chip_select_logic_1__0x0c), .RD(RD), .WD(WD), .S0(S0), .S1(S1), .S2(S2), .S3(S3), .S4(S4),
    .S5(S5), .S6(S6), .S7(S7), .S0_2(n1_byte_ram_13_s0_2), .S1_2(n1_byte_ram_13_s1_2),
    .S2_2(n1_byte_ram_13_s2_2), .S3_2(n1_byte_ram_13_s3_2), .S4_2(n1_byte_ram_13_s4_2),
    .S5_2(n1_byte_ram_13_s5_2), .S6_2(n1_byte_ram_13_s6_2), .S7_2(n1_byte_ram_13_s7_2));
  _1_Byte_ram u_1_byte_ram_14 (
    .AD(ram_chip_select_logic_1__0x0d), .RD(RD), .WD(WD), .S0(S0), .S1(S1), .S2(S2), .S3(S3), .S4(S4),
    .S5(S5), .S6(S6), .S7(S7), .S0_2(n1_byte_ram_14_s0_2), .S1_2(n1_byte_ram_14_s1_2),
    .S2_2(n1_byte_ram_14_s2_2), .S3_2(n1_byte_ram_14_s3_2), .S4_2(n1_byte_ram_14_s4_2),
    .S5_2(n1_byte_ram_14_s5_2), .S6_2(n1_byte_ram_14_s6_2), .S7_2(n1_byte_ram_14_s7_2));
  _1_Byte_ram u_1_byte_ram_15 (
    .AD(or_4_out), .RD(RD), .WD(or_9_out), .S0(not_4_out), .S1(not_7_out), .S2(not_5_out), .S3(not_6_out),
    .S4(not_3_out), .S5(not_2_out), .S6(not_1_out), .S7(not_29_out), .S0_2(n1_byte_ram_15_s0_2),
    .S1_2(n1_byte_ram_15_s1_2), .S2_2(n1_byte_ram_15_s2_2), .S3_2(n1_byte_ram_15_s3_2),
    .S4_2(n1_byte_ram_15_s4_2), .S5_2(n1_byte_ram_15_s5_2), .S6_2(n1_byte_ram_15_s6_2),
    .S7_2(n1_byte_ram_15_s7_2));
  _1_Byte_ram u_1_byte_ram_16 (
    .AD(1'b1), .RD(1'b1), .WD(and_1_out), .S0(S0), .S1(S1), .S2(S2), .S3(S3), .S4(S4), .S5(S5), .S6(S6),
    .S7(S7), .S0_2(OUT0), .S1_2(OUT1), .S2_2(OUT2), .S3_2(OUT3), .S4_2(OUT4), .S5_2(OUT5), .S6_2(OUT6),
    .S7_2(OUT7));
  _8_Bit_OR u_8_bit_or_2 (
    .A0(n1_byte_ram_1_s0_2), .B0(n1_byte_ram_2_s0_2), .A1(n1_byte_ram_1_s1_2), .B1(n1_byte_ram_2_s1_2),
    .A2(n1_byte_ram_1_s2_2), .B2(n1_byte_ram_2_s2_2), .A3(n1_byte_ram_1_s3_2), .B3(n1_byte_ram_2_s3_2),
    .A4(n1_byte_ram_1_s4_2), .B4(n1_byte_ram_2_s4_2), .A5(n1_byte_ram_1_s5_2), .B5(n1_byte_ram_2_s5_2),
    .A6(n1_byte_ram_1_s6_2), .B6(n1_byte_ram_2_s6_2), .A7(n1_byte_ram_1_s7_2), .B7(n1_byte_ram_2_s7_2),
    .S0(n8_bit_or_2_s0), .S1(n8_bit_or_2_s1), .S2(n8_bit_or_2_s2), .S3(n8_bit_or_2_s3), .S4(n8_bit_or_2_s4),
    .S5(n8_bit_or_2_s5), .S6(n8_bit_or_2_s6), .S7(n8_bit_or_2_s7));
  _8_Bit_OR u_8_bit_or_3 (
    .A0(n1_byte_ram_3_s0_2), .B0(n1_byte_ram_4_s0_2), .A1(n1_byte_ram_3_s1_2), .B1(n1_byte_ram_4_s1_2),
    .A2(n1_byte_ram_3_s2_2), .B2(n1_byte_ram_4_s2_2), .A3(n1_byte_ram_3_s3_2), .B3(n1_byte_ram_4_s3_2),
    .A4(n1_byte_ram_3_s4_2), .B4(n1_byte_ram_4_s4_2), .A5(n1_byte_ram_3_s5_2), .B5(n1_byte_ram_4_s5_2),
    .A6(n1_byte_ram_3_s6_2), .B6(n1_byte_ram_4_s6_2), .A7(n1_byte_ram_3_s7_2), .B7(n1_byte_ram_4_s7_2),
    .S0(n8_bit_or_3_s0), .S1(n8_bit_or_3_s1), .S2(n8_bit_or_3_s2), .S3(n8_bit_or_3_s3), .S4(n8_bit_or_3_s4),
    .S5(n8_bit_or_3_s5), .S6(n8_bit_or_3_s6), .S7(n8_bit_or_3_s7));
  _8_Bit_OR u_8_bit_or_4 (
    .A0(n1_byte_ram_5_s0_2), .B0(n1_byte_ram_6_s0_2), .A1(n1_byte_ram_5_s1_2), .B1(n1_byte_ram_6_s1_2),
    .A2(n1_byte_ram_5_s2_2), .B2(n1_byte_ram_6_s2_2), .A3(n1_byte_ram_5_s3_2), .B3(n1_byte_ram_6_s3_2),
    .A4(n1_byte_ram_5_s4_2), .B4(n1_byte_ram_6_s4_2), .A5(n1_byte_ram_5_s5_2), .B5(n1_byte_ram_6_s5_2),
    .A6(n1_byte_ram_5_s6_2), .B6(n1_byte_ram_6_s6_2), .A7(n1_byte_ram_5_s7_2), .B7(n1_byte_ram_6_s7_2),
    .S0(n8_bit_or_4_s0), .S1(n8_bit_or_4_s1), .S2(n8_bit_or_4_s2), .S3(n8_bit_or_4_s3), .S4(n8_bit_or_4_s4),
    .S5(n8_bit_or_4_s5), .S6(n8_bit_or_4_s6), .S7(n8_bit_or_4_s7));
  _8_Bit_OR u_8_bit_or_5 (
    .A0(n1_byte_ram_7_s0_2), .B0(n1_byte_ram_8_s0_2), .A1(n1_byte_ram_7_s1_2), .B1(n1_byte_ram_8_s1_2),
    .A2(n1_byte_ram_7_s2_2), .B2(n1_byte_ram_8_s2_2), .A3(n1_byte_ram_7_s3_2), .B3(n1_byte_ram_8_s3_2),
    .A4(n1_byte_ram_7_s4_2), .B4(n1_byte_ram_8_s4_2), .A5(n1_byte_ram_7_s5_2), .B5(n1_byte_ram_8_s5_2),
    .A6(n1_byte_ram_7_s6_2), .B6(n1_byte_ram_8_s6_2), .A7(n1_byte_ram_7_s7_2), .B7(n1_byte_ram_8_s7_2),
    .S0(n8_bit_or_5_s0), .S1(n8_bit_or_5_s1), .S2(n8_bit_or_5_s2), .S3(n8_bit_or_5_s3), .S4(n8_bit_or_5_s4),
    .S5(n8_bit_or_5_s5), .S6(n8_bit_or_5_s6), .S7(n8_bit_or_5_s7));
  _8_Bit_OR u_8_bit_or_6 (
    .A0(n1_byte_ram_9_s0_2), .B0(n1_byte_ram_10_s0_2), .A1(n1_byte_ram_9_s1_2), .B1(n1_byte_ram_10_s1_2),
    .A2(n1_byte_ram_9_s2_2), .B2(n1_byte_ram_10_s2_2), .A3(n1_byte_ram_9_s3_2), .B3(n1_byte_ram_10_s3_2),
    .A4(n1_byte_ram_9_s4_2), .B4(n1_byte_ram_10_s4_2), .A5(n1_byte_ram_9_s5_2), .B5(n1_byte_ram_10_s5_2),
    .A6(n1_byte_ram_9_s6_2), .B6(n1_byte_ram_10_s6_2), .A7(n1_byte_ram_9_s7_2), .B7(n1_byte_ram_10_s7_2),
    .S0(n8_bit_or_6_s0), .S1(n8_bit_or_6_s1), .S2(n8_bit_or_6_s2), .S3(n8_bit_or_6_s3), .S4(n8_bit_or_6_s4),
    .S5(n8_bit_or_6_s5), .S6(n8_bit_or_6_s6), .S7(n8_bit_or_6_s7));
  _8_Bit_OR u_8_bit_or_7 (
    .A0(n1_byte_ram_11_s0_2), .B0(n1_byte_ram_12_s0_2), .A1(n1_byte_ram_11_s1_2), .B1(n1_byte_ram_12_s1_2),
    .A2(n1_byte_ram_11_s2_2), .B2(n1_byte_ram_12_s2_2), .A3(n1_byte_ram_11_s3_2), .B3(n1_byte_ram_12_s3_2),
    .A4(n1_byte_ram_11_s4_2), .B4(n1_byte_ram_12_s4_2), .A5(n1_byte_ram_11_s5_2), .B5(n1_byte_ram_12_s5_2),
    .A6(n1_byte_ram_11_s6_2), .B6(n1_byte_ram_12_s6_2), .A7(n1_byte_ram_11_s7_2), .B7(n1_byte_ram_12_s7_2),
    .S0(n8_bit_or_7_s0), .S1(n8_bit_or_7_s1), .S2(n8_bit_or_7_s2), .S3(n8_bit_or_7_s3), .S4(n8_bit_or_7_s4),
    .S5(n8_bit_or_7_s5), .S6(n8_bit_or_7_s6), .S7(n8_bit_or_7_s7));
  _8_Bit_OR u_8_bit_or_8 (
    .A0(n1_byte_ram_13_s0_2), .B0(n1_byte_ram_14_s0_2), .A1(n1_byte_ram_13_s1_2), .B1(n1_byte_ram_14_s1_2),
    .A2(n1_byte_ram_13_s2_2), .B2(n1_byte_ram_14_s2_2), .A3(n1_byte_ram_13_s3_2), .B3(n1_byte_ram_14_s3_2),
    .A4(n1_byte_ram_13_s4_2), .B4(n1_byte_ram_14_s4_2), .A5(n1_byte_ram_13_s5_2), .B5(n1_byte_ram_14_s5_2),
    .A6(n1_byte_ram_13_s6_2), .B6(n1_byte_ram_14_s6_2), .A7(n1_byte_ram_13_s7_2), .B7(n1_byte_ram_14_s7_2),
    .S0(n8_bit_or_8_s0), .S1(n8_bit_or_8_s1), .S2(n8_bit_or_8_s2), .S3(n8_bit_or_8_s3), .S4(n8_bit_or_8_s4),
    .S5(n8_bit_or_8_s5), .S6(n8_bit_or_8_s6), .S7(n8_bit_or_8_s7));
  _8_Bit_OR u_8_bit_or_9 (
    .A0(n8_bit_or_2_s0), .B0(n8_bit_or_3_s0), .A1(n8_bit_or_2_s1), .B1(n8_bit_or_3_s1), .A2(n8_bit_or_2_s2),
    .B2(n8_bit_or_3_s2), .A3(n8_bit_or_2_s3), .B3(n8_bit_or_3_s3), .A4(n8_bit_or_2_s4), .B4(n8_bit_or_3_s4),
    .A5(n8_bit_or_2_s5), .B5(n8_bit_or_3_s5), .A6(n8_bit_or_2_s6), .B6(n8_bit_or_3_s6), .A7(n8_bit_or_2_s7),
    .B7(n8_bit_or_3_s7), .S0(n8_bit_or_9_s0), .S1(n8_bit_or_9_s1), .S2(n8_bit_or_9_s2), .S3(n8_bit_or_9_s3),
    .S4(n8_bit_or_9_s4), .S5(n8_bit_or_9_s5), .S6(n8_bit_or_9_s6), .S7(n8_bit_or_9_s7));
  _8_Bit_OR u_8_bit_or_10 (
    .A0(n8_bit_or_4_s0), .B0(n8_bit_or_5_s0), .A1(n8_bit_or_4_s1), .B1(n8_bit_or_5_s1), .A2(n8_bit_or_4_s2),
    .B2(n8_bit_or_5_s2), .A3(n8_bit_or_4_s3), .B3(n8_bit_or_5_s3), .A4(n8_bit_or_4_s4), .B4(n8_bit_or_5_s4),
    .A5(n8_bit_or_4_s5), .B5(n8_bit_or_5_s5), .A6(n8_bit_or_4_s6), .B6(n8_bit_or_5_s6), .A7(n8_bit_or_4_s7),
    .B7(n8_bit_or_5_s7), .S0(n8_bit_or_10_s0), .S1(n8_bit_or_10_s1), .S2(n8_bit_or_10_s2),
    .S3(n8_bit_or_10_s3), .S4(n8_bit_or_10_s4), .S5(n8_bit_or_10_s5), .S6(n8_bit_or_10_s6),
    .S7(n8_bit_or_10_s7));
  _8_Bit_OR u_8_bit_or_11 (
    .A0(n8_bit_or_6_s0), .B0(n8_bit_or_7_s0), .A1(n8_bit_or_6_s1), .B1(n8_bit_or_7_s1), .A2(n8_bit_or_6_s2),
    .B2(n8_bit_or_7_s2), .A3(n8_bit_or_6_s3), .B3(n8_bit_or_7_s3), .A4(n8_bit_or_6_s4), .B4(n8_bit_or_7_s4),
    .A5(n8_bit_or_6_s5), .B5(n8_bit_or_7_s5), .A6(n8_bit_or_6_s6), .B6(n8_bit_or_7_s6), .A7(n8_bit_or_6_s7),
    .B7(n8_bit_or_7_s7), .S0(n8_bit_or_11_s0), .S1(n8_bit_or_11_s1), .S2(n8_bit_or_11_s2),
    .S3(n8_bit_or_11_s3), .S4(n8_bit_or_11_s4), .S5(n8_bit_or_11_s5), .S6(n8_bit_or_11_s6),
    .S7(n8_bit_or_11_s7));
  _8_Bit_OR u_8_bit_or_12 (
    .A0(n8_bit_or_8_s0), .B0(n1_byte_ram_15_s0_2), .A1(n8_bit_or_8_s1), .B1(n1_byte_ram_15_s1_2),
    .A2(n8_bit_or_8_s2), .B2(n1_byte_ram_15_s2_2), .A3(n8_bit_or_8_s3), .B3(n1_byte_ram_15_s3_2),
    .A4(n8_bit_or_8_s4), .B4(n1_byte_ram_15_s4_2), .A5(n8_bit_or_8_s5), .B5(n1_byte_ram_15_s5_2),
    .A6(n8_bit_or_8_s6), .B6(n1_byte_ram_15_s6_2), .A7(n8_bit_or_8_s7), .B7(n1_byte_ram_15_s7_2),
    .S0(n8_bit_or_12_s0), .S1(n8_bit_or_12_s1), .S2(n8_bit_or_12_s2), .S3(n8_bit_or_12_s3),
    .S4(n8_bit_or_12_s4), .S5(n8_bit_or_12_s5), .S6(n8_bit_or_12_s6), .S7(n8_bit_or_12_s7));
  _8_Bit_OR u_8_bit_or_13 (
    .A0(n8_bit_or_9_s0), .B0(n8_bit_or_10_s0), .A1(n8_bit_or_9_s1), .B1(n8_bit_or_10_s1),
    .A2(n8_bit_or_9_s2), .B2(n8_bit_or_10_s2), .A3(n8_bit_or_9_s3), .B3(n8_bit_or_10_s3),
    .A4(n8_bit_or_9_s4), .B4(n8_bit_or_10_s4), .A5(n8_bit_or_9_s5), .B5(n8_bit_or_10_s5),
    .A6(n8_bit_or_9_s6), .B6(n8_bit_or_10_s6), .A7(n8_bit_or_9_s7), .B7(n8_bit_or_10_s7),
    .S0(n8_bit_or_13_s0), .S1(n8_bit_or_13_s1), .S2(n8_bit_or_13_s2), .S3(n8_bit_or_13_s3),
    .S4(n8_bit_or_13_s4), .S5(n8_bit_or_13_s5), .S6(n8_bit_or_13_s6), .S7(n8_bit_or_13_s7));
  _8_Bit_OR u_8_bit_or_14 (
    .A0(n8_bit_or_11_s0), .B0(n8_bit_or_12_s0), .A1(n8_bit_or_11_s1), .B1(n8_bit_or_12_s1),
    .A2(n8_bit_or_11_s2), .B2(n8_bit_or_12_s2), .A3(n8_bit_or_11_s3), .B3(n8_bit_or_12_s3),
    .A4(n8_bit_or_11_s4), .B4(n8_bit_or_12_s4), .A5(n8_bit_or_11_s5), .B5(n8_bit_or_12_s5),
    .A6(n8_bit_or_11_s6), .B6(n8_bit_or_12_s6), .A7(n8_bit_or_11_s7), .B7(n8_bit_or_12_s7),
    .S0(n8_bit_or_14_s0), .S1(n8_bit_or_14_s1), .S2(n8_bit_or_14_s2), .S3(n8_bit_or_14_s3),
    .S4(n8_bit_or_14_s4), .S5(n8_bit_or_14_s5), .S6(n8_bit_or_14_s6), .S7(n8_bit_or_14_s7));
  _8_Bit_OR u_8_bit_or_15 (
    .A0(n8_bit_or_13_s0), .B0(n8_bit_or_14_s0), .A1(n8_bit_or_13_s1), .B1(n8_bit_or_14_s1),
    .A2(n8_bit_or_13_s2), .B2(n8_bit_or_14_s2), .A3(n8_bit_or_13_s3), .B3(n8_bit_or_14_s3),
    .A4(n8_bit_or_13_s4), .B4(n8_bit_or_14_s4), .A5(n8_bit_or_13_s5), .B5(n8_bit_or_14_s5),
    .A6(n8_bit_or_13_s6), .B6(n8_bit_or_14_s6), .A7(n8_bit_or_13_s7), .B7(n8_bit_or_14_s7), .S0(S0_2),
    .S1(S1_2), .S2(S2_2), .S3(S3_2), .S4(S4_2), .S5(S5_2), .S6(S6_2), .S7(S7_2));
endmodule

module ALU_ADD_CONTROL (
  input  ADD,
  input  AND,
  input  OR,
  input  SLB,
  input  SRB,
  input  JPZ,
  input  JPC,
  output ALU0,
  output ALU1,
  output ALU2
);

  wire and_1_out, and_2_out, and_3_out, and_4_out, and_5_out, and_6_out, and_7_out, and_8_out, and_9_out,
       and_10_out, and_11_out, and_12_out, and_13_out, and_14_out, and_15_out, and_16_out, and_17_out,
       and_18_out, and_19_out, and_20_out, and_21_out, and_22_out, and_23_out, and_24_out, and_25_out,
       and_26_out, and_27_out, and_28_out, and_29_out, and_30_out, and_31_out, and_32_out, and_33_out,
       and_34_out, and_35_out, and_36_out, and_37_out, and_38_out, and_39_out, and_40_out, and_41_out,
       and_42_out, and_43_out, and_44_out, and_45_out, and_46_out, and_47_out, and_48_out, and_49_out,
       and_50_out, and_51_out, and_52_out, and_53_out, and_54_out, and_55_out, and_56_out, and_57_out,
       and_58_out, and_59_out, and_60_out, and_61_out, and_62_out, and_63_out, and_64_out, and_65_out,
       and_66_out, and_67_out, and_68_out, and_69_out, and_70_out, and_71_out, and_72_out, not_1_out,
       not_2_out, not_3_out, not_4_out, not_5_out, not_6_out, not_7_out, not_8_out, not_9_out, not_10_out,
       not_11_out, not_12_out, not_13_out, not_14_out, not_15_out, not_16_out, not_17_out, not_18_out,
       not_19_out, not_20_out, not_21_out, not_22_out, not_23_out, not_24_out, not_25_out, not_26_out,
       not_27_out, not_28_out, not_29_out, not_30_out, not_31_out, not_32_out, not_33_out, not_34_out,
       not_35_out, not_36_out, not_37_out, not_38_out, not_39_out, not_40_out, not_41_out, not_42_out,
       not_43_out, not_44_out, not_45_out, not_46_out, not_47_out, not_48_out, not_49_out, not_50_out,
       not_51_out, not_52_out, not_53_out, not_54_out, not_55_out, not_56_out, not_57_out, not_58_out,
       not_59_out, not_60_out, not_61_out, not_62_out, not_63_out, not_64_out, not_65_out, not_66_out,
       not_67_out, not_68_out, not_69_out, not_70_out, not_71_out, not_72_out, or_1_out, or_2_out, or_3_out,
       or_4_out, or_5_out, or_6_out;

  not not_1 (not_1_out, ADD);
  not not_2 (not_2_out, AND);
  not not_3 (not_3_out, OR);
  not not_4 (not_4_out, SLB);
  not not_5 (not_5_out, SRB);
  not not_6 (not_6_out, JPZ);
  not not_7 (not_7_out, ADD);
  not not_8 (not_8_out, AND);
  not not_9 (not_9_out, OR);
  not not_10 (not_10_out, SLB);
  not not_11 (not_11_out, JPZ);
  not not_12 (not_12_out, ADD);
  not not_13 (not_13_out, AND);
  not not_14 (not_14_out, SLB);
  not not_15 (not_15_out, SRB);
  not not_16 (not_16_out, JPZ);
  not not_17 (not_17_out, AND);
  not not_18 (not_18_out, OR);
  not not_19 (not_19_out, SLB);
  not not_20 (not_20_out, SRB);
  not not_21 (not_21_out, JPZ);
  not not_22 (not_22_out, ADD);
  not not_23 (not_23_out, AND);
  not not_24 (not_24_out, OR);
  not not_25 (not_25_out, SLB);
  not not_26 (not_26_out, SRB);
  not not_27 (not_27_out, JPZ);
  not not_28 (not_28_out, ADD);
  not not_29 (not_29_out, AND);
  not not_30 (not_30_out, OR);
  not not_31 (not_31_out, SLB);
  not not_32 (not_32_out, SRB);
  not not_33 (not_33_out, ADD);
  not not_34 (not_34_out, AND);
  not not_35 (not_35_out, SLB);
  not not_36 (not_36_out, SRB);
  not not_37 (not_37_out, JPZ);
  not not_38 (not_38_out, ADD);
  not not_39 (not_39_out, OR);
  not not_40 (not_40_out, SLB);
  not not_41 (not_41_out, SRB);
  not not_42 (not_42_out, JPZ);
  not not_43 (not_43_out, ADD);
  not not_44 (not_44_out, AND);
  not not_45 (not_45_out, OR);
  not not_46 (not_46_out, SLB);
  not not_47 (not_47_out, SRB);
  not not_48 (not_48_out, JPZ);
  not not_49 (not_49_out, ADD);
  not not_50 (not_50_out, AND);
  not not_51 (not_51_out, OR);
  not not_52 (not_52_out, SLB);
  not not_53 (not_53_out, SRB);
  not not_54 (not_54_out, ADD);
  not not_55 (not_55_out, AND);
  not not_56 (not_56_out, OR);
  not not_57 (not_57_out, SLB);
  not not_58 (not_58_out, JPZ);
  not not_59 (not_59_out, ADD);
  not not_60 (not_60_out, AND);
  not not_61 (not_61_out, OR);
  not not_62 (not_62_out, SRB);
  not not_63 (not_63_out, JPZ);
  and and_1 (and_1_out, not_1_out, not_2_out);
  and and_2 (and_2_out, not_3_out, not_4_out);
  and and_3 (and_3_out, not_5_out, not_6_out);
  and and_4 (and_4_out, not_7_out, not_8_out);
  and and_5 (and_5_out, not_9_out, not_10_out);
  and and_6 (and_6_out, SRB, not_11_out);
  not not_64 (not_64_out, JPC);
  and and_7 (and_7_out, not_12_out, not_13_out);
  and and_8 (and_8_out, OR, not_14_out);
  and and_9 (and_9_out, not_15_out, not_16_out);
  not not_65 (not_65_out, JPC);
  and and_10 (and_10_out, ADD, not_17_out);
  and and_11 (and_11_out, not_18_out, not_19_out);
  and and_12 (and_12_out, not_20_out, not_21_out);
  not not_66 (not_66_out, JPC);
  and and_13 (and_13_out, not_22_out, not_23_out);
  and and_14 (and_14_out, not_24_out, not_25_out);
  and and_15 (and_15_out, not_26_out, not_27_out);
  and and_16 (and_16_out, not_28_out, not_29_out);
  and and_17 (and_17_out, not_30_out, not_31_out);
  and and_18 (and_18_out, not_32_out, JPZ);
  not not_67 (not_67_out, JPC);
  and and_19 (and_19_out, not_33_out, not_34_out);
  and and_20 (and_20_out, OR, not_35_out);
  and and_21 (and_21_out, not_36_out, not_37_out);
  not not_68 (not_68_out, JPC);
  and and_22 (and_22_out, not_38_out, AND);
  and and_23 (and_23_out, not_39_out, not_40_out);
  and and_24 (and_24_out, not_41_out, not_42_out);
  not not_69 (not_69_out, JPC);
  and and_25 (and_25_out, not_43_out, not_44_out);
  and and_26 (and_26_out, not_45_out, not_46_out);
  and and_27 (and_27_out, not_47_out, not_48_out);
  and and_28 (and_28_out, not_49_out, not_50_out);
  and and_29 (and_29_out, not_51_out, not_52_out);
  and and_30 (and_30_out, not_53_out, JPZ);
  not not_70 (not_70_out, JPC);
  and and_31 (and_31_out, not_54_out, not_55_out);
  and and_32 (and_32_out, not_56_out, not_57_out);
  and and_33 (and_33_out, SRB, not_58_out);
  not not_71 (not_71_out, JPC);
  and and_34 (and_34_out, not_59_out, not_60_out);
  and and_35 (and_35_out, not_61_out, SLB);
  and and_36 (and_36_out, not_62_out, not_63_out);
  not not_72 (not_72_out, JPC);
  and and_37 (and_37_out, and_1_out, and_2_out);
  and and_38 (and_38_out, and_3_out, JPC);
  and and_39 (and_39_out, and_4_out, and_5_out);
  and and_40 (and_40_out, and_6_out, not_64_out);
  and and_41 (and_41_out, and_7_out, and_8_out);
  and and_42 (and_42_out, and_9_out, not_65_out);
  and and_43 (and_43_out, and_10_out, and_11_out);
  and and_44 (and_44_out, and_12_out, not_66_out);
  and and_45 (and_45_out, and_13_out, and_14_out);
  and and_46 (and_46_out, and_15_out, JPC);
  and and_47 (and_47_out, and_16_out, and_17_out);
  and and_48 (and_48_out, and_18_out, not_67_out);
  and and_49 (and_49_out, and_19_out, and_20_out);
  and and_50 (and_50_out, and_21_out, not_68_out);
  and and_51 (and_51_out, and_22_out, and_23_out);
  and and_52 (and_52_out, and_24_out, not_69_out);
  and and_53 (and_53_out, and_25_out, and_26_out);
  and and_54 (and_54_out, and_27_out, JPC);
  and and_55 (and_55_out, and_28_out, and_29_out);
  and and_56 (and_56_out, and_30_out, not_70_out);
  and and_57 (and_57_out, and_31_out, and_32_out);
  and and_58 (and_58_out, and_33_out, not_71_out);
  and and_59 (and_59_out, and_34_out, and_35_out);
  and and_60 (and_60_out, and_36_out, not_72_out);
  and and_61 (and_61_out, and_37_out, and_38_out);
  and and_62 (and_62_out, and_39_out, and_40_out);
  and and_63 (and_63_out, and_41_out, and_42_out);
  and and_64 (and_64_out, and_43_out, and_44_out);
  and and_65 (and_65_out, and_45_out, and_46_out);
  and and_66 (and_66_out, and_47_out, and_48_out);
  and and_67 (and_67_out, and_49_out, and_50_out);
  and and_68 (and_68_out, and_51_out, and_52_out);
  and and_69 (and_69_out, and_53_out, and_54_out);
  and and_70 (and_70_out, and_55_out, and_56_out);
  and and_71 (and_71_out, and_57_out, and_58_out);
  and and_72 (and_72_out, and_59_out, and_60_out);
  or or_1 (or_1_out, and_61_out, and_62_out);
  or or_2 (or_2_out, and_63_out, and_64_out);
  or or_3 (or_3_out, and_65_out, and_66_out);
  or or_4 (or_4_out, and_67_out, and_68_out);
  or or_5 (or_5_out, and_69_out, and_70_out);
  or or_6 (or_6_out, and_71_out, and_72_out);
  or or_7 (ALU0, or_1_out, or_2_out);
  or or_8 (ALU1, or_3_out, or_4_out);
  or or_9 (ALU2, or_5_out, or_6_out);
endmodule

module ALU (
  input  A0,
  input  A1,
  input  A2,
  input  A3,
  input  A4,
  input  A5,
  input  A6,
  input  A7,
  input  B0,
  input  B1,
  input  B2,
  input  B3,
  input  B4,
  input  B5,
  input  B6,
  input  B7,
  input  C0,
  input  C1,
  input  C2,
  output JPC,
  output JPZ,
  output S0,
  output S1,
  output S2,
  output S3,
  output S4,
  output S5,
  output S6,
  output S7
);

  wire alu_add_logic_1_a0_2, alu_add_logic_1_a1_2, alu_add_logic_1_a2_2, alu_add_logic_1_a3_2,
       alu_add_logic_1_a4_2, alu_add_logic_1_a5_2, alu_add_logic_1_a6_2, alu_add_logic_1_a7_2,
       alu_add_logic_1_b0_2, alu_add_logic_1_b1_2, alu_add_logic_1_b2_2, alu_add_logic_1_b3_2,
       alu_add_logic_1_b4_2, alu_add_logic_1_b5_2, alu_add_logic_1_b6_2, alu_add_logic_1_b7_2,
       alu_and_logic_1_a0_2, alu_and_logic_1_a1_2, alu_and_logic_1_a2_2, alu_and_logic_1_a3_2,
       alu_and_logic_1_a4_2, alu_and_logic_1_a5_2, alu_and_logic_1_a6_2, alu_and_logic_1_a7_2,
       alu_and_logic_1_b0_2, alu_and_logic_1_b1_2, alu_and_logic_1_b2_2, alu_and_logic_1_b3_2,
       alu_and_logic_1_b4_2, alu_and_logic_1_b5_2, alu_and_logic_1_b6_2, alu_and_logic_1_b7_2,
       alu_or_logic_1_a0_2, alu_or_logic_1_a1_2, alu_or_logic_1_a2_2, alu_or_logic_1_a3_2,
       alu_or_logic_1_a4_2, alu_or_logic_1_a5_2, alu_or_logic_1_a6_2, alu_or_logic_1_a7_2,
       alu_or_logic_1_b0_2, alu_or_logic_1_b1_2, alu_or_logic_1_b2_2, alu_or_logic_1_b3_2,
       alu_or_logic_1_b4_2, alu_or_logic_1_b5_2, alu_or_logic_1_b6_2, alu_or_logic_1_b7_2, n8_bit_adder_1_c7,
       n8_bit_adder_1_s0, n8_bit_adder_1_s1, n8_bit_adder_1_s2, n8_bit_adder_1_s3, n8_bit_adder_1_s4,
       n8_bit_adder_1_s5, n8_bit_adder_1_s6, n8_bit_adder_1_s7, n8_bit_and_1_s0, n8_bit_and_1_s1,
       n8_bit_and_1_s2, n8_bit_and_1_s3, n8_bit_and_1_s4, n8_bit_and_1_s5, n8_bit_and_1_s6, n8_bit_and_1_s7,
       n8_bit_or_1_s0, n8_bit_or_1_s1, n8_bit_or_1_s2, n8_bit_or_1_s3, n8_bit_or_1_s4, n8_bit_or_1_s5,
       n8_bit_or_1_s6, n8_bit_or_1_s7, n8_bit_or_2_s0, n8_bit_or_2_s1, n8_bit_or_2_s2, n8_bit_or_2_s3,
       n8_bit_or_2_s4, n8_bit_or_2_s5, n8_bit_or_2_s6, n8_bit_or_2_s7, n8_bit_or_3_s0, n8_bit_or_3_s1,
       n8_bit_or_3_s2, n8_bit_or_3_s3, n8_bit_or_3_s4, n8_bit_or_3_s5, n8_bit_or_3_s6, n8_bit_or_3_s7,
       n8_bit_or_4_s0, n8_bit_or_4_s1, n8_bit_or_4_s2, n8_bit_or_4_s3, n8_bit_or_4_s4, n8_bit_or_4_s5,
       n8_bit_or_4_s6, n8_bit_or_4_s7, n8_bit_shift_left_1_c7, n8_bit_shift_left_1_s0,
       n8_bit_shift_left_1_s1, n8_bit_shift_left_1_s2, n8_bit_shift_left_1_s3, n8_bit_shift_left_1_s4,
       n8_bit_shift_left_1_s5, n8_bit_shift_left_1_s6, n8_bit_shift_left_1_s7, n8_bit_shift_right_1_c7,
       n8_bit_shift_right_1_s0, n8_bit_shift_right_1_s1, n8_bit_shift_right_1_s2, n8_bit_shift_right_1_s3,
       n8_bit_shift_right_1_s4, n8_bit_shift_right_1_s5, n8_bit_shift_right_1_s6, n8_bit_shift_right_1_s7,
       or_1_out;

  ALU_ADD_LOGIC alu_add_logic_1 (
    .A0(A0), .A1(A1), .A2(A2), .A3(A3), .A4(A4), .A5(A5), .A6(A6), .A7(A7), .B0(B0), .B1(B1), .B2(B2),
    .B3(B3), .B4(B4), .B5(B5), .B6(B6), .B7(B7), .C0(C0), .C1(C1), .C2(C2), .A0_2(alu_add_logic_1_a0_2),
    .B0_2(alu_add_logic_1_b0_2), .A1_2(alu_add_logic_1_a1_2), .B1_2(alu_add_logic_1_b1_2),
    .A2_2(alu_add_logic_1_a2_2), .B2_2(alu_add_logic_1_b2_2), .A3_2(alu_add_logic_1_a3_2),
    .B3_2(alu_add_logic_1_b3_2), .A4_2(alu_add_logic_1_a4_2), .B4_2(alu_add_logic_1_b4_2),
    .A5_2(alu_add_logic_1_a5_2), .B5_2(alu_add_logic_1_b5_2), .A6_2(alu_add_logic_1_a6_2),
    .B6_2(alu_add_logic_1_b6_2), .A7_2(alu_add_logic_1_a7_2), .B7_2(alu_add_logic_1_b7_2));  // open: JPZ, JPC
  ALU_AND_LOGIC alu_and_logic_1 (
    .A0(A0), .A1(A1), .A2(A2), .A3(A3), .A4(A4), .A5(A5), .A6(A6), .A7(A7), .B0(B0), .B1(B1), .B2(B2),
    .B3(B3), .B4(B4), .B5(B5), .B6(B6), .B7(B7), .C0(C0), .C1(C1), .C2(C2), .A0_2(alu_and_logic_1_a0_2),
    .B0_2(alu_and_logic_1_b0_2), .A1_2(alu_and_logic_1_a1_2), .B1_2(alu_and_logic_1_b1_2),
    .A2_2(alu_and_logic_1_a2_2), .B2_2(alu_and_logic_1_b2_2), .A3_2(alu_and_logic_1_a3_2),
    .B3_2(alu_and_logic_1_b3_2), .A4_2(alu_and_logic_1_a4_2), .B4_2(alu_and_logic_1_b4_2),
    .A5_2(alu_and_logic_1_a5_2), .B5_2(alu_and_logic_1_b5_2), .A6_2(alu_and_logic_1_a6_2),
    .B6_2(alu_and_logic_1_b6_2), .A7_2(alu_and_logic_1_a7_2), .B7_2(alu_and_logic_1_b7_2));
  ALU_OR_LOGIC alu_or_logic_1 (
    .A0(A0), .A1(A1), .A2(A2), .A3(A3), .A4(A4), .A5(A5), .A6(A6), .A7(A7), .B0(B0), .B1(B1), .B2(B2),
    .B3(B3), .B4(B4), .B5(B5), .B6(B6), .B7(B7), .C0(C0), .C1(C1), .C2(C2), .A0_2(alu_or_logic_1_a0_2),
    .B0_2(alu_or_logic_1_b0_2), .A1_2(alu_or_logic_1_a1_2), .B1_2(alu_or_logic_1_b1_2),
    .A2_2(alu_or_logic_1_a2_2), .B2_2(alu_or_logic_1_b2_2), .A3_2(alu_or_logic_1_a3_2),
    .B3_2(alu_or_logic_1_b3_2), .A4_2(alu_or_logic_1_a4_2), .B4_2(alu_or_logic_1_b4_2),
    .A5_2(alu_or_logic_1_a5_2), .B5_2(alu_or_logic_1_b5_2), .A6_2(alu_or_logic_1_a6_2),
    .B6_2(alu_or_logic_1_b6_2), .A7_2(alu_or_logic_1_a7_2), .B7_2(alu_or_logic_1_b7_2));
  _8_Bit_SHIFT_LEFT u_8_bit_shift_left_1 (
    .A0(A0), .A1(A1), .A2(A2), .A3(A3), .A4(A4), .A5(A5), .A6(A6), .A7(A7), .S0(n8_bit_shift_left_1_s0),
    .S1(n8_bit_shift_left_1_s1), .S2(n8_bit_shift_left_1_s2), .S3(n8_bit_shift_left_1_s3),
    .S4(n8_bit_shift_left_1_s4), .S5(n8_bit_shift_left_1_s5), .S6(n8_bit_shift_left_1_s6),
    .S7(n8_bit_shift_left_1_s7), .C7(n8_bit_shift_left_1_c7), .C0(C0), .C1(C1), .C2(C2));
  _8_Bit_SHIFT_RIGHT u_8_bit_shift_right_1 (
    .A0(A0), .A1(A1), .A2(A2), .A3(A3), .A4(A4), .A5(A5), .A6(A6), .A7(A7), .C7(n8_bit_shift_right_1_c7),
    .S0(n8_bit_shift_right_1_s0), .S1(n8_bit_shift_right_1_s1), .S2(n8_bit_shift_right_1_s2),
    .S3(n8_bit_shift_right_1_s3), .S4(n8_bit_shift_right_1_s4), .S5(n8_bit_shift_right_1_s5),
    .S6(n8_bit_shift_right_1_s6), .S7(n8_bit_shift_right_1_s7), .C0(C0), .C1(C1), .C2(C2));
  or or_1 (or_1_out, n8_bit_shift_left_1_c7, n8_bit_shift_right_1_c7);
  JPZ_Logic jpz_logic_1 (
    .S0(n8_bit_adder_1_s0), .S1(n8_bit_adder_1_s1), .S2(n8_bit_adder_1_s2), .S3(n8_bit_adder_1_s3),
    .S4(n8_bit_adder_1_s4), .S5(n8_bit_adder_1_s5), .S6(n8_bit_adder_1_s6), .S7(n8_bit_adder_1_s7),
    .C7(n8_bit_adder_1_c7), .JPZ(JPZ));
  _8_Bit_Adder u_8_bit_adder_1 (
    .A0(alu_add_logic_1_a0_2), .B0(alu_add_logic_1_b0_2), .A1(alu_add_logic_1_a1_2),
    .B1(alu_add_logic_1_b1_2), .A2(alu_add_logic_1_a2_2), .B2(alu_add_logic_1_b2_2),
    .A3(alu_add_logic_1_a3_2), .B3(alu_add_logic_1_b3_2), .A4(alu_add_logic_1_a4_2),
    .B4(alu_add_logic_1_b4_2), .A5(alu_add_logic_1_a5_2), .B5(alu_add_logic_1_b5_2),
    .A6(alu_add_logic_1_a6_2), .B6(alu_add_logic_1_b6_2), .A7(alu_add_logic_1_a7_2),
    .B7(alu_add_logic_1_b7_2), .S0(n8_bit_adder_1_s0), .S1(n8_bit_adder_1_s1), .S2(n8_bit_adder_1_s2),
    .S3(n8_bit_adder_1_s3), .S4(n8_bit_adder_1_s4), .S5(n8_bit_adder_1_s5), .S6(n8_bit_adder_1_s6),
    .S7(n8_bit_adder_1_s7), .C7(n8_bit_adder_1_c7));
  _8_Bit_AND u_8_bit_and_1 (
    .A0(alu_and_logic_1_a0_2), .B0(alu_and_logic_1_b0_2), .A1(alu_and_logic_1_a1_2),
    .B1(alu_and_logic_1_b1_2), .A2(alu_and_logic_1_a2_2), .B2(alu_and_logic_1_b2_2),
    .A3(alu_and_logic_1_a3_2), .B3(alu_and_logic_1_b3_2), .A4(alu_and_logic_1_a4_2),
    .B4(alu_and_logic_1_b4_2), .A5(alu_and_logic_1_a5_2), .B5(alu_and_logic_1_b5_2),
    .A6(alu_and_logic_1_a6_2), .B6(alu_and_logic_1_b6_2), .A7(alu_and_logic_1_a7_2),
    .B7(alu_and_logic_1_b7_2), .S0(n8_bit_and_1_s0), .S1(n8_bit_and_1_s1), .S2(n8_bit_and_1_s2),
    .S3(n8_bit_and_1_s3), .S4(n8_bit_and_1_s4), .S5(n8_bit_and_1_s5), .S6(n8_bit_and_1_s6),
    .S7(n8_bit_and_1_s7));
  _8_Bit_OR u_8_bit_or_1 (
    .A0(alu_or_logic_1_a0_2), .B0(alu_or_logic_1_b0_2), .A1(alu_or_logic_1_a1_2), .B1(alu_or_logic_1_b1_2),
    .A2(alu_or_logic_1_a2_2), .B2(alu_or_logic_1_b2_2), .A3(alu_or_logic_1_a3_2), .B3(alu_or_logic_1_b3_2),
    .A4(alu_or_logic_1_a4_2), .B4(alu_or_logic_1_b4_2), .A5(alu_or_logic_1_a5_2), .B5(alu_or_logic_1_b5_2),
    .A6(alu_or_logic_1_a6_2), .B6(alu_or_logic_1_b6_2), .A7(alu_or_logic_1_a7_2), .B7(alu_or_logic_1_b7_2),
    .S0(n8_bit_or_1_s0), .S1(n8_bit_or_1_s1), .S2(n8_bit_or_1_s2), .S3(n8_bit_or_1_s3), .S4(n8_bit_or_1_s4),
    .S5(n8_bit_or_1_s5), .S6(n8_bit_or_1_s6), .S7(n8_bit_or_1_s7));
  or or_2 (JPC, or_1_out, n8_bit_adder_1_c7);
  _8_Bit_OR u_8_bit_or_2 (
    .A0(n8_bit_adder_1_s0), .B0(n8_bit_and_1_s0), .A1(n8_bit_adder_1_s1), .B1(n8_bit_and_1_s1),
    .A2(n8_bit_adder_1_s2), .B2(n8_bit_and_1_s2), .A3(n8_bit_adder_1_s3), .B3(n8_bit_and_1_s3),
    .A4(n8_bit_adder_1_s4), .B4(n8_bit_and_1_s4), .A5(n8_bit_adder_1_s5), .B5(n8_bit_and_1_s5),
    .A6(n8_bit_adder_1_s6), .B6(n8_bit_and_1_s6), .A7(n8_bit_adder_1_s7), .B7(n8_bit_and_1_s7),
    .S0(n8_bit_or_2_s0), .S1(n8_bit_or_2_s1), .S2(n8_bit_or_2_s2), .S3(n8_bit_or_2_s3), .S4(n8_bit_or_2_s4),
    .S5(n8_bit_or_2_s5), .S6(n8_bit_or_2_s6), .S7(n8_bit_or_2_s7));
  _8_Bit_OR u_8_bit_or_3 (
    .A0(n8_bit_or_1_s0), .B0(n8_bit_shift_left_1_s0), .A1(n8_bit_or_1_s1), .B1(n8_bit_shift_left_1_s1),
    .A2(n8_bit_or_1_s2), .B2(n8_bit_shift_left_1_s2), .A3(n8_bit_or_1_s3), .B3(n8_bit_shift_left_1_s3),
    .A4(n8_bit_or_1_s4), .B4(n8_bit_shift_left_1_s4), .A5(n8_bit_or_1_s5), .B5(n8_bit_shift_left_1_s5),
    .A6(n8_bit_or_1_s6), .B6(n8_bit_shift_left_1_s6), .A7(n8_bit_or_1_s7), .B7(n8_bit_shift_left_1_s7),
    .S0(n8_bit_or_3_s0), .S1(n8_bit_or_3_s1), .S2(n8_bit_or_3_s2), .S3(n8_bit_or_3_s3), .S4(n8_bit_or_3_s4),
    .S5(n8_bit_or_3_s5), .S6(n8_bit_or_3_s6), .S7(n8_bit_or_3_s7));
  _8_Bit_OR u_8_bit_or_4 (
    .A0(n8_bit_or_2_s0), .B0(n8_bit_or_3_s0), .A1(n8_bit_or_2_s1), .B1(n8_bit_or_3_s1), .A2(n8_bit_or_2_s2),
    .B2(n8_bit_or_3_s2), .A3(n8_bit_or_2_s3), .B3(n8_bit_or_3_s3), .A4(n8_bit_or_2_s4), .B4(n8_bit_or_3_s4),
    .A5(n8_bit_or_2_s5), .B5(n8_bit_or_3_s5), .A6(n8_bit_or_2_s6), .B6(n8_bit_or_3_s6), .A7(n8_bit_or_2_s7),
    .B7(n8_bit_or_3_s7), .S0(n8_bit_or_4_s0), .S1(n8_bit_or_4_s1), .S2(n8_bit_or_4_s2), .S3(n8_bit_or_4_s3),
    .S4(n8_bit_or_4_s4), .S5(n8_bit_or_4_s5), .S6(n8_bit_or_4_s6), .S7(n8_bit_or_4_s7));
  _8_Bit_OR u_8_bit_or_5 (
    .A0(n8_bit_or_4_s0), .B0(n8_bit_shift_right_1_s0), .A1(n8_bit_or_4_s1), .B1(n8_bit_shift_right_1_s1),
    .A2(n8_bit_or_4_s2), .B2(n8_bit_shift_right_1_s2), .A3(n8_bit_or_4_s3), .B3(n8_bit_shift_right_1_s3),
    .A4(n8_bit_or_4_s4), .B4(n8_bit_shift_right_1_s4), .A5(n8_bit_or_4_s5), .B5(n8_bit_shift_right_1_s5),
    .A6(n8_bit_or_4_s6), .B6(n8_bit_shift_right_1_s6), .A7(n8_bit_or_4_s7), .B7(n8_bit_shift_right_1_s7),
    .S0(S0), .S1(S1), .S2(S2), .S3(S3), .S4(S4), .S5(S5), .S6(S6), .S7(S7));
endmodule

module CONTROL (
  input  S0,
  input  S1,
  input  S2,
  input  S3,
  input  S4,
  input  S5,
  input  S6,
  input  S7,
  input  CK,
  input  WR0,
  input  WR1,
  input  WR2,
  input  WR3,
  input  WR4,
  input  WR5,
  input  WR6,
  input  WR7,
  input  MEM0,
  input  MEM1,
  input  MEM2,
  input  MEM3,
  input  MEM4,
  input  MEM5,
  input  MEM6,
  input  MEM7,
  input  JPZ,
  input  JPC,
  output WR0_2,
  output WR1_2,
  output WR2_2,
  output WR3_2,
  output WR4_2,
  output WR5_2,
  output WR6_2,
  output WR7_2,
  output LD,
  output A0,
  output A1,
  output A2,
  output A3,
  output RD,
  output WD,
  output RAM0,
  output RAM1,
  output RAM2,
  output RAM3,
  output RAM4,
  output RAM5,
  output RAM6,
  output RAM7,
  output ALU0,
  output ALU_1,
  output ALU2,
  output ALUA0,
  output ALUA1,
  output ALUA2,
  output ALUA3,
  output ALUA4,
  output ALUA5,
  output ALUA6,
  output ALUA7,
  output ALUB0,
  output ALUB1,
  output ALUB2,
  output ALUB3,
  output ALUB4,
  output ALUB5,
  output ALUB6,
  output ALUB7,
  output JPZ_2,
  output JPC_2,
  output A0_2,
  output A1_2,
  output A2_2,
  output A3_2,
  output A4,
  output A5,
  output A6,
  output A7
);

  wire and_1_out, and_2_out, and_3_out, and_4_out, and_5_out, and_6_out, and_7_out, and_8_out, and_9_out,
       and_10_out, and_11_out, and_12_out, and_13_out, and_14_out, and_15_out, and_16_out, and_17_out,
       and_18_out, and_19_out, and_20_out, and_21_out, and_22_out, and_23_out, and_24_out, and_25_out,
       and_26_out, and_27_out, and_28_out, and_29_out, and_30_out, and_31_out, and_32_out, and_33_out,
       and_34_out, and_35_out, and_36_out, and_37_out, and_38_out, and_39_out, and_40_out, and_41_out,
       and_42_out, and_43_out, and_44_out, and_45_out, and_46_out, and_48_out, and_49_out, and_50_out,
       and_51_out, and_52_out, and_53_out, and_54_out, and_55_out, and_57_out, and_58_out, and_59_out,
       and_60_out, and_61_out, and_62_out, and_63_out, and_64_out, and_65_out, and_66_out, and_67_out,
       and_68_out, and_69_out, and_70_out, and_71_out, and_72_out, and_73_out, and_74_out, and_75_out,
       and_76_out, and_77_out, and_78_out, and_79_out, and_80_out, and_81_out, and_82_out, and_83_out,
       and_84_out, and_85_out, and_86_out, and_87_out, and_88_out, and_89_out, and_90_out, and_91_out,
       and_92_out, and_93_out, and_102_out, and_103_out, and_104_out, and_105_out, and_106_out, and_107_out,
       and_108_out, and_109_out, and_110_out, and_111_out, and_112_out, and_113_out, and_114_out,
       and_115_out, and_116_out, and_117_out, and_127_out, and_128_out, and_129_out, and_130_out,
       and_131_out, and_132_out, and_133_out, and_134_out, and_135_out, and_136_out, and_137_out,
       and_138_out, and_139_out, and_140_out, and_141_out, and_142_out, d_ff_1_q, d_ff_2_q, d_ff_3_q,
       d_ff_4_q, d_ff_5_q, d_ff_6_q, n8_bit_or_1_s0, n8_bit_or_1_s1, n8_bit_or_1_s2, n8_bit_or_1_s3,
       n8_bit_or_1_s4, n8_bit_or_1_s5, n8_bit_or_1_s6, n8_bit_or_1_s7, n8_bit_or_2_s0, n8_bit_or_2_s1,
       n8_bit_or_2_s2, n8_bit_or_2_s3, n8_bit_or_2_s4, n8_bit_or_2_s5, n8_bit_or_2_s6, n8_bit_or_2_s7,
       n8_bit_or_3_s0, n8_bit_or_3_s1, n8_bit_or_3_s2, n8_bit_or_3_s3, n8_bit_or_3_s4, n8_bit_or_3_s5,
       n8_bit_or_3_s6, n8_bit_or_3_s7, not_1_out, not_2_out, not_3_out, not_4_out, not_5_out, not_6_out,
       not_7_out, not_8_out, not_9_out, not_10_out, not_11_out, not_12_out, not_13_out, not_14_out,
       not_15_out, not_16_out, not_17_out, not_18_out, not_19_out, not_20_out, not_21_out, not_22_out,
       not_23_out, not_24_out, not_25_out, not_26_out, not_27_out, not_28_out, not_29_out, not_30_out,
       not_31_out, not_32_out, not_33_out, not_34_out, not_35_out, not_36_out, not_37_out, not_38_out,
       not_39_out, not_40_out, not_41_out, not_42_out, not_43_out, not_44_out, not_45_out, not_46_out,
       not_47_out, not_48_out, not_49_out, not_50_out, not_51_out, or_1_out, or_2_out, or_3_out, or_4_out,
       or_5_out, or_6_out, or_7_out, or_8_out, or_9_out, or_10_out, or_11_out, or_12_out, or_13_out,
       or_14_out, or_15_out, or_16_out, or_17_out, or_18_out, or_19_out, or_20_out, or_21_out, or_22_out,
       sign_extension_1_s0_2, sign_extension_1_s1_2, sign_extension_1_s2_2, sign_extension_1_s3_2,
       sign_extension_1_s4, sign_extension_1_s5, sign_extension_1_s6, sign_extension_1_s7,
       sign_extension_2_s0_2, sign_extension_2_s1_2, sign_extension_2_s2_2, sign_extension_2_s3_2,
       sign_extension_2_s4, sign_extension_2_s5, sign_extension_2_s6, sign_extension_2_s7;

  or or_1 (or_1_out, or_3_out, or_2_out);
  or or_2 (or_2_out, d_ff_3_q, d_ff_2_q);
  or or_3 (or_3_out, or_4_out, d_ff_4_q);
  or or_4 (or_4_out, d_ff_6_q, d_ff_5_q);
  or or_5 (or_5_out, or_1_out, d_ff_1_q);
  not not_1 (not_1_out, S1);
  not not_2 (not_2_out, S2);
  not not_3 (not_3_out, S3);
  not not_4 (not_4_out, S0);
  not not_5 (not_5_out, S2);
  not not_6 (not_6_out, S3);
  Sign_Extension sign_extension_1 (
    .S0(S4), .S1(S5), .S2(S6), .S3(S7), .S0_2(sign_extension_1_s0_2), .S1_2(sign_extension_1_s1_2),
    .S2_2(sign_extension_1_s2_2), .S3_2(sign_extension_1_s3_2), .S4(sign_extension_1_s4),
    .S5(sign_extension_1_s5), .S6(sign_extension_1_s6), .S7(sign_extension_1_s7));
  not not_7 (not_7_out, S2);
  not not_8 (not_8_out, S3);
  not not_9 (not_9_out, S0);
  not not_10 (not_10_out, S1);
  not not_11 (not_11_out, S3);
  not not_12 (not_12_out, S1);
  not not_13 (not_13_out, S3);
  not not_14 (not_14_out, S1);
  not not_15 (not_15_out, S2);
  not not_16 (not_16_out, S2);
  not not_17 (not_17_out, S0);
  not not_18 (not_18_out, S3);
  not not_19 (not_19_out, S0);
  not not_20 (not_20_out, S2);
  not not_21 (not_21_out, S0);
  not not_22 (not_22_out, S1);
  not not_23 (not_23_out, S3);
  not not_24 (not_24_out, S0);
  not not_25 (not_25_out, S1);
  not not_26 (not_26_out, S2);
  not not_27 (not_27_out, S0);
  not not_28 (not_28_out, S1);
  not not_29 (not_29_out, or_5_out);
  and and_1 (and_1_out, S0, not_1_out);
  and and_2 (and_2_out, and_1_out, and_3_out);
  and and_3 (and_3_out, not_2_out, not_3_out);
  D_Flip_Flop #(.trigger("falling")) d_ff_1 (.clk(CK), .D(and_45_out), .Q(d_ff_1_q));  // open: Qn, preset, en, reset
  not not_30 (not_30_out, or_5_out);
  and and_4 (and_4_out, not_4_out, S1);
  and and_5 (and_5_out, and_4_out, and_6_out);
  and and_6 (and_6_out, not_5_out, not_6_out);
  not not_31 (not_31_out, or_5_out);
  and and_7 (and_7_out, S0, S1);
  and and_8 (and_8_out, and_7_out, and_9_out);
  and and_9 (and_9_out, not_7_out, not_8_out);
  not not_32 (not_32_out, or_5_out);
  and and_10 (and_10_out, not_9_out, not_10_out);
  and and_11 (and_11_out, and_10_out, and_12_out);
  and and_12 (and_12_out, S2, not_11_out);
  not not_33 (not_33_out, or_5_out);
  and and_13 (and_13_out, S0, not_12_out);
  and and_14 (and_14_out, and_13_out, and_15_out);
  and and_15 (and_15_out, S2, not_13_out);
  not not_34 (not_34_out, or_5_out);
  and and_16 (and_16_out, S0, not_14_out);
  and and_17 (and_17_out, and_16_out, and_18_out);
  and and_18 (and_18_out, not_15_out, S3);
  not not_35 (not_35_out, or_5_out);
  and and_19 (and_19_out, S0, S1);
  and and_20 (and_20_out, and_19_out, and_21_out);
  and and_21 (and_21_out, not_16_out, S3);
  Sign_Extension sign_extension_2 (
    .S0(S4), .S1(S5), .S2(S6), .S3(S7), .S0_2(sign_extension_2_s0_2), .S1_2(sign_extension_2_s1_2),
    .S2_2(sign_extension_2_s2_2), .S3_2(sign_extension_2_s3_2), .S4(sign_extension_2_s4),
    .S5(sign_extension_2_s5), .S6(sign_extension_2_s6), .S7(sign_extension_2_s7));
  not not_36 (not_36_out, or_5_out);
  and and_22 (and_22_out, not_17_out, S1);
  and and_23 (and_23_out, and_22_out, and_24_out);
  and and_24 (and_24_out, S2, not_18_out);
  D_Flip_Flop #(.trigger("falling")) d_ff_2 (.clk(CK), .D(and_52_out), .Q(d_ff_2_q));  // open: Qn, preset, en, reset
  not not_37 (not_37_out, or_5_out);
  and and_25 (and_25_out, not_19_out, S1);
  and and_26 (and_26_out, and_25_out, and_27_out);
  and and_27 (and_27_out, not_20_out, S3);
  D_Flip_Flop #(.trigger("falling")) d_ff_3 (.clk(CK), .D(and_53_out), .Q(d_ff_3_q));  // open: Qn, preset, en, reset
  not not_38 (not_38_out, or_5_out);
  and and_28 (and_28_out, not_21_out, not_22_out);
  and and_29 (and_29_out, and_28_out, and_30_out);
  and and_30 (and_30_out, S2, S3);
  D_Flip_Flop #(.trigger("falling")) d_ff_4 (.clk(CK), .D(and_54_out), .Q(d_ff_4_q));  // open: Qn, preset, en, reset
  not not_39 (not_39_out, or_5_out);
  and and_31 (and_31_out, S0, S1);
  and and_32 (and_32_out, and_31_out, and_33_out);
  and and_33 (and_33_out, S2, not_23_out);
  D_Flip_Flop #(.trigger("falling")) d_ff_5 (.clk(CK), .D(and_55_out), .Q(d_ff_5_q));  // open: Qn, preset, en, reset
  not not_40 (not_40_out, or_5_out);
  and and_34 (and_34_out, not_24_out, not_25_out);
  and and_35 (and_35_out, not_26_out, S3);
  D_Flip_Flop #(.trigger("falling")) d_ff_6 (.clk(CK), .D(and_57_out), .Q(d_ff_6_q));  // open: Qn, preset, en, reset
  not not_41 (not_41_out, or_5_out);
  and and_36 (and_36_out, not_27_out, S1);
  and and_37 (and_37_out, and_36_out, and_38_out);
  and and_38 (and_38_out, S2, S3);
  not not_42 (not_42_out, or_5_out);
  and and_39 (and_39_out, S0, S1);
  and and_40 (and_40_out, and_39_out, and_41_out);
  and and_41 (and_41_out, S2, S3);
  not not_43 (not_43_out, or_5_out);
  and and_42 (and_42_out, S0, not_28_out);
  and and_43 (and_43_out, and_42_out, and_44_out);
  and and_44 (and_44_out, S2, S3);
  and and_45 (and_45_out, not_29_out, and_2_out);
  and and_46 (and_46_out, not_30_out, and_5_out);
  and and_47 (RD, not_31_out, and_8_out);
  and and_48 (and_48_out, not_32_out, and_11_out);
  and and_49 (and_49_out, not_33_out, and_14_out);
  and and_50 (and_50_out, not_34_out, and_17_out);
  or or_6 (or_6_out, and_49_out, and_50_out);
  and and_51 (and_51_out, not_35_out, and_20_out);
  or or_7 (or_7_out, or_6_out, and_51_out);
  and and_52 (and_52_out, not_36_out, and_23_out);
  and and_53 (and_53_out, not_37_out, and_26_out);
  or or_8 (or_8_out, d_ff_3_q, d_ff_2_q);
  and and_54 (and_54_out, not_38_out, and_29_out);
  or or_9 (or_9_out, d_ff_4_q, or_8_out);
  and and_55 (and_55_out, not_39_out, and_32_out);
  and and_56 (JPZ_2, d_ff_5_q, JPZ);
  and and_57 (and_57_out, not_40_out, and_58_out);
  and and_58 (and_58_out, and_34_out, and_35_out);
  and and_59 (and_59_out, not_41_out, and_37_out);
  and and_60 (and_60_out, not_42_out, and_40_out);
  or or_10 (or_10_out, and_60_out, and_59_out);
  and and_61 (and_61_out, not_43_out, and_43_out);
  not not_44 (not_44_out, WR0);
  not not_45 (not_45_out, WR1);
  not not_46 (not_46_out, WR2);
  not not_47 (not_47_out, WR3);
  not not_48 (not_48_out, WR4);
  not not_49 (not_49_out, WR5);
  not not_50 (not_50_out, WR6);
  not not_51 (not_51_out, WR7);
  and and_62 (and_62_out, d_ff_1_q, S0);
  and and_63 (and_63_out, d_ff_1_q, S1);
  and and_64 (and_64_out, d_ff_1_q, S2);
  and and_65 (and_65_out, d_ff_1_q, S3);
  and and_66 (and_66_out, d_ff_1_q, S4);
  and and_67 (and_67_out, d_ff_1_q, S5);
  and and_68 (and_68_out, d_ff_1_q, S6);
  and and_69 (and_69_out, d_ff_1_q, S7);
  and and_70 (and_70_out, sign_extension_1_s0_2, and_46_out);
  and and_71 (and_71_out, sign_extension_1_s1_2, and_46_out);
  and and_72 (and_72_out, sign_extension_1_s2_2, and_46_out);
  and and_73 (and_73_out, sign_extension_1_s3_2, and_46_out);
  and and_74 (and_74_out, sign_extension_1_s4, and_46_out);
  and and_75 (and_75_out, sign_extension_1_s5, and_46_out);
  and and_76 (and_76_out, sign_extension_1_s6, and_46_out);
  and and_77 (and_77_out, sign_extension_1_s7, and_46_out);
  and and_78 (and_78_out, RD, S4);
  and and_79 (and_79_out, RD, S5);
  and and_80 (and_80_out, RD, S6);
  and and_81 (and_81_out, RD, S7);
  and and_82 (and_82_out, RD, MEM0);
  and and_83 (and_83_out, RD, MEM1);
  and and_84 (and_84_out, RD, MEM2);
  and and_85 (and_85_out, RD, MEM3);
  and and_86 (and_86_out, RD, MEM4);
  and and_87 (and_87_out, RD, MEM5);
  and and_88 (and_88_out, RD, MEM6);
  and and_89 (and_89_out, RD, MEM7);
  and and_90 (and_90_out, and_48_out, S4);
  and and_91 (and_91_out, and_48_out, S5);
  and and_92 (and_92_out, and_48_out, S6);
  and and_93 (and_93_out, and_48_out, S7);
  and and_94 (RAM0, and_48_out, WR0);
  and and_95 (RAM1, and_48_out, WR1);
  and and_96 (RAM2, and_48_out, WR2);
  and and_97 (RAM3, and_48_out, WR3);
  and and_98 (RAM4, and_48_out, WR4);
  and and_99 (RAM5, and_48_out, WR5);
  and and_100 (RAM6, and_48_out, WR6);
  and and_101 (RAM7, and_48_out, WR7);
  or or_11 (or_11_out, and_51_out, d_ff_4_q);
  and and_102 (and_102_out, or_7_out, sign_extension_2_s0_2);
  and and_103 (and_103_out, or_7_out, sign_extension_2_s1_2);
  and and_104 (and_104_out, or_7_out, sign_extension_2_s2_2);
  and and_105 (and_105_out, or_7_out, sign_extension_2_s3_2);
  and and_106 (and_106_out, or_7_out, sign_extension_2_s4);
  and and_107 (and_107_out, or_7_out, sign_extension_2_s5);
  and and_108 (and_108_out, or_7_out, sign_extension_2_s6);
  and and_109 (and_109_out, or_7_out, sign_extension_2_s7);
  and and_110 (and_110_out, or_9_out, S0);
  and and_111 (and_111_out, or_9_out, S1);
  and and_112 (and_112_out, or_9_out, S2);
  and and_113 (and_113_out, or_9_out, S3);
  and and_114 (and_114_out, or_9_out, S4);
  and and_115 (and_115_out, or_9_out, S5);
  and and_116 (and_116_out, or_9_out, S6);
  and and_117 (and_117_out, or_9_out, S7);
  and and_118 (JPC_2, JPC, d_ff_6_q);
  or or_12 (or_12_out, d_ff_6_q, d_ff_5_q);
  and and_119 (A0_2, or_12_out, S0);
  and and_120 (A1_2, or_12_out, S1);
  and and_121 (A2_2, or_12_out, S2);
  and and_122 (A3_2, or_12_out, S3);
  and and_123 (A4, or_12_out, S4);
  and and_124 (A5, or_12_out, S5);
  and and_125 (A6, or_12_out, S6);
  and and_126 (A7, or_12_out, S7);
  and and_127 (and_127_out, or_10_out, WR0);
  and and_128 (and_128_out, or_10_out, WR1);
  and and_129 (and_129_out, or_10_out, WR2);
  and and_130 (and_130_out, or_10_out, WR3);
  and and_131 (and_131_out, or_10_out, WR4);
  and and_132 (and_132_out, or_10_out, WR5);
  and and_133 (and_133_out, or_10_out, WR6);
  and and_134 (and_134_out, or_10_out, WR7);
  and and_135 (and_135_out, and_61_out, not_44_out);
  and and_136 (and_136_out, and_61_out, not_45_out);
  and and_137 (and_137_out, and_61_out, not_46_out);
  and and_138 (and_138_out, and_61_out, not_47_out);
  and and_139 (and_139_out, and_61_out, not_48_out);
  and and_140 (and_140_out, and_61_out, not_49_out);
  and and_141 (and_141_out, and_61_out, not_50_out);
  and and_142 (and_142_out, and_61_out, not_51_out);
  _8_Bit_OR u_8_bit_or_1 (
    .A0(and_62_out), .B0(and_70_out), .A1(and_63_out), .B1(and_71_out), .A2(and_64_out), .B2(and_72_out),
    .A3(and_65_out), .B3(and_73_out), .A4(and_66_out), .B4(and_74_out), .A5(and_67_out), .B5(and_75_out),
    .A6(and_68_out), .B6(and_76_out), .A7(and_69_out), .B7(and_77_out), .S0(n8_bit_or_1_s0),
    .S1(n8_bit_or_1_s1), .S2(n8_bit_or_1_s2), .S3(n8_bit_or_1_s3), .S4(n8_bit_or_1_s4), .S5(n8_bit_or_1_s5),
    .S6(n8_bit_or_1_s6), .S7(n8_bit_or_1_s7));
  or or_13 (or_13_out, RD, or_20_out);
  or or_14 (or_14_out, and_50_out, d_ff_3_q);
  or or_15 (or_15_out, d_ff_2_q, and_49_out);
  or or_16 (or_16_out, d_ff_1_q, and_46_out);
  or or_17 (or_17_out, or_16_out, or_13_out);
  and and_143 (WD, CK, and_48_out);
  or or_18 (or_18_out, or_11_out, or_15_out);
  ALU_ADD_CONTROL alu_add_control_1 (
    .OR(or_11_out), .SLB(and_59_out), .SRB(and_60_out), .ADD(or_15_out), .AND(or_14_out), .JPZ(1'b0),
    .JPC(1'b0), .ALU0(ALU0), .ALU1(ALU_1), .ALU2(ALU2));
  or or_19 (or_19_out, and_60_out, and_59_out);
  and and_144 (LD, or_17_out, CK);
  or or_20 (or_20_out, or_18_out, or_21_out);
  or or_21 (or_21_out, or_14_out, or_22_out);
  or or_22 (or_22_out, or_19_out, and_61_out);
  _8_Bit_OR u_8_bit_or_2 (
    .A0(and_102_out), .B0(and_110_out), .A1(and_103_out), .B1(and_111_out), .A2(and_104_out),
    .B2(and_112_out), .A3(and_105_out), .B3(and_113_out), .A4(and_106_out), .B4(and_114_out),
    .A5(and_107_out), .B5(and_115_out), .A6(and_108_out), .B6(and_116_out), .A7(and_109_out),
    .B7(and_117_out), .S0(n8_bit_or_2_s0), .S1(n8_bit_or_2_s1), .S2(n8_bit_or_2_s2), .S3(n8_bit_or_2_s3),
    .S4(n8_bit_or_2_s4), .S5(n8_bit_or_2_s5), .S6(n8_bit_or_2_s6), .S7(n8_bit_or_2_s7));
  _8_Bit_OR u_8_bit_or_3 (
    .A0(n8_bit_or_1_s0), .B0(and_82_out), .A1(n8_bit_or_1_s1), .B1(and_83_out), .A2(n8_bit_or_1_s2),
    .B2(and_84_out), .A3(n8_bit_or_1_s3), .B3(and_85_out), .A4(n8_bit_or_1_s4), .B4(and_86_out),
    .A5(n8_bit_or_1_s5), .B5(and_87_out), .A6(n8_bit_or_1_s6), .B6(and_88_out), .A7(n8_bit_or_1_s7),
    .B7(and_89_out), .S0(n8_bit_or_3_s0), .S1(n8_bit_or_3_s1), .S2(n8_bit_or_3_s2), .S3(n8_bit_or_3_s3),
    .S4(n8_bit_or_3_s4), .S5(n8_bit_or_3_s5), .S6(n8_bit_or_3_s6), .S7(n8_bit_or_3_s7));
  or or_23 (A0, and_90_out, and_78_out);
  or or_24 (A1, and_91_out, and_79_out);
  or or_25 (A2, and_92_out, and_80_out);
  or or_26 (A3, and_93_out, and_81_out);
  _8_Bit_OR u_8_bit_or_4 (
    .A0(n8_bit_or_2_s0), .B0(and_127_out), .A1(n8_bit_or_2_s1), .B1(and_128_out), .A2(n8_bit_or_2_s2),
    .B2(and_129_out), .A3(n8_bit_or_2_s3), .B3(and_130_out), .A4(n8_bit_or_2_s4), .B4(and_131_out),
    .A5(n8_bit_or_2_s5), .B5(and_132_out), .A6(n8_bit_or_2_s6), .B6(and_133_out), .A7(n8_bit_or_2_s7),
    .B7(and_134_out), .S0(ALUA0), .S1(ALUA1), .S2(ALUA2), .S3(ALUA3), .S4(ALUA4), .S5(ALUA5), .S6(ALUA6),
    .S7(ALUA7));
  _8_Bit_OR u_8_bit_or_5 (
    .A0(n8_bit_or_3_s0), .B0(and_135_out), .A1(n8_bit_or_3_s1), .B1(and_136_out), .A2(n8_bit_or_3_s2),
    .B2(and_137_out), .A3(n8_bit_or_3_s3), .B3(and_138_out), .A4(n8_bit_or_3_s4), .B4(and_139_out),
    .A5(n8_bit_or_3_s5), .B5(and_140_out), .A6(n8_bit_or_3_s6), .B6(and_141_out), .A7(n8_bit_or_3_s7),
    .B7(and_142_out), .S0(WR0_2), .S1(WR1_2), .S2(WR2_2), .S3(WR3_2), .S4(WR4_2), .S5(WR5_2), .S6(WR6_2),
    .S7(WR7_2));

  assign ALUB0 = WR0;
  assign ALUB1 = WR1;
  assign ALUB2 = WR2;
  assign ALUB3 = WR3;
  assign ALUB4 = WR4;
  assign ALUB5 = WR5;
  assign ALUB6 = WR6;
  assign ALUB7 = WR7;

  // Notes on the sheet:
  //   ANDI
  //   ORI
  //   ORN
  //   ADDI
  //   ADDN
  //   ANDN
  //   JPZ
  //   JPC
  //   SLB
  //   SRB
  //   NOT
endmodule

module Control_Circuit (
  input  CK,
  input  WR0,
  input  WR1,
  input  WR2,
  input  WR3,
  input  WR4,
  input  WR5,
  input  WR6,
  input  WR7,
  input  S0,
  input  S1,
  input  S2,
  input  S3,
  input  S4,
  input  S5,
  input  S6,
  input  S7,
  output A0,
  output A1,
  output A2,
  output A3,
  output A4,
  output A5,
  output A6,
  output A7,
  output B0,
  output B1,
  output B2,
  output B3,
  output B4,
  output B5,
  output B6,
  output B7,
  output ALU2,
  output ALU_1,
  output ALU_0,
  output A0_2,
  output A1_2,
  output A2_2,
  output A3_2,
  output WD,
  output S0_2,
  output S1_2,
  output S2_2,
  output S3_2,
  output S4_2,
  output S5_2,
  output S6_2,
  output S7_2,
  output WR0_2,
  output WR1_2,
  output WR2_2,
  output WR3_2,
  output WR4_2,
  output WR5_2,
  output WR6_2,
  output WR7_2,
  output LD
);

  wire and_1_out, and_2_out, and_3_out, and_4_out, and_5_out, and_6_out, and_7_out, and_8_out, and_9_out,
       and_10_out, and_11_out, and_12_out, and_13_out, and_14_out, and_15_out, and_16_out, and_17_out,
       and_18_out, and_19_out, and_20_out, and_21_out, and_22_out, and_23_out, and_24_out, and_25_out,
       and_26_out, and_27_out, and_28_out, and_29_out, and_30_out, and_31_out, and_32_out, and_33_out,
       and_34_out, and_35_out, and_36_out, and_45_out, and_46_out, and_47_out, and_48_out, and_49_out,
       and_50_out, and_51_out, and_52_out, and_53_out, and_54_out, and_55_out, and_56_out, and_57_out,
       and_58_out, and_59_out, and_60_out, and_61_out, and_62_out, and_63_out, and_64_out, and_65_out,
       and_66_out, and_67_out, and_68_out, and_69_out, and_70_out, and_71_out, and_72_out, and_73_out,
       d_ff_1_q, d_ff_2_q, d_ff_3_q, not_1_out, not_2_out, not_3_out, not_4_out, not_5_out, not_6_out,
       not_7_out, not_8_out, not_9_out, not_10_out, not_11_out, not_12_out, not_13_out, not_14_out,
       not_15_out, not_16_out, not_17_out, not_18_out, not_19_out, not_20_out, not_21_out, or_1_out,
       or_2_out, sign_extension_1_s0_2, sign_extension_1_s1_2, sign_extension_1_s2_2, sign_extension_1_s3_2,
       sign_extension_1_s4, sign_extension_1_s5, sign_extension_1_s6, sign_extension_1_s7;

  not not_1 (not_1_out, S0);
  not not_2 (not_2_out, S3);
  not not_3 (not_3_out, S1);
  not not_4 (not_4_out, S3);
  not not_5 (not_5_out, S2);
  not not_6 (not_6_out, S3);
  not not_7 (not_7_out, S0);
  not not_8 (not_8_out, S1);
  not not_9 (not_9_out, S3);
  not not_10 (not_10_out, S1);
  not not_11 (not_11_out, S2);
  not not_12 (not_12_out, S3);
  or or_1 (or_1_out, d_ff_3_q, d_ff_2_q);
  not not_13 (not_13_out, S0);
  not not_14 (not_14_out, S2);
  not not_15 (not_15_out, S3);
  D_Flip_Flop #(.trigger("falling")) d_ff_1 (.clk(CK), .D(and_25_out), .Q(d_ff_1_q));  // open: Qn, preset, en, reset
  not not_16 (not_16_out, or_1_out);
  and and_1 (and_1_out, not_1_out, S1);
  and and_2 (and_2_out, S2, not_2_out);
  not not_17 (not_17_out, or_1_out);
  and and_3 (and_3_out, S0, not_3_out);
  and and_4 (and_4_out, S2, not_4_out);
  D_Flip_Flop #(.trigger("falling")) d_ff_2 (.clk(CK), .D(and_45_out), .Q(d_ff_2_q));  // open: Qn, preset, en, reset
  not not_18 (not_18_out, or_1_out);
  and and_5 (and_5_out, S0, S1);
  and and_6 (and_6_out, not_5_out, not_6_out);
  not not_19 (not_19_out, or_1_out);
  and and_7 (and_7_out, not_7_out, not_8_out);
  and and_8 (and_8_out, S2, not_9_out);
  D_Flip_Flop #(.trigger("falling")) d_ff_3 (.clk(CK), .D(and_49_out), .Q(d_ff_3_q));  // open: Qn, preset, en, reset
  not not_20 (not_20_out, or_1_out);
  and and_9 (and_9_out, S0, not_10_out);
  and and_10 (and_10_out, not_11_out, not_12_out);
  and and_11 (and_11_out, or_1_out, S0);
  and and_12 (and_12_out, or_1_out, S1);
  and and_13 (and_13_out, or_1_out, S2);
  and and_14 (and_14_out, or_1_out, S3);
  and and_15 (and_15_out, or_1_out, S4);
  and and_16 (and_16_out, or_1_out, S5);
  and and_17 (and_17_out, or_1_out, S6);
  and and_18 (and_18_out, or_1_out, S7);
  not not_21 (not_21_out, or_1_out);
  and and_19 (and_19_out, not_13_out, S1);
  and and_20 (and_20_out, not_14_out, not_15_out);
  and and_21 (and_21_out, and_51_out, S4);
  and and_22 (and_22_out, and_51_out, S5);
  and and_23 (and_23_out, and_51_out, S6);
  and and_24 (and_24_out, and_51_out, S7);
  and and_25 (and_25_out, not_16_out, and_26_out);
  and and_26 (and_26_out, and_1_out, and_2_out);
  and and_27 (and_27_out, not_17_out, and_28_out);
  and and_28 (and_28_out, and_3_out, and_4_out);
  and and_29 (and_29_out, and_47_out, S4);
  and and_30 (and_30_out, and_47_out, S5);
  and and_31 (and_31_out, and_47_out, S6);
  and and_32 (and_32_out, and_47_out, S7);
  and and_33 (and_33_out, d_ff_2_q, S0);
  and and_34 (and_34_out, d_ff_2_q, S1);
  and and_35 (and_35_out, d_ff_2_q, S2);
  and and_36 (and_36_out, d_ff_2_q, S3);
  and and_37 (S0_2, d_ff_2_q, WR0);
  and and_38 (S1_2, WD, WR1);
  and and_39 (S2_2, WD, WR2);
  and and_40 (S3_2, WD, WR3);
  and and_41 (S4_2, WD, WR4);
  and and_42 (S5_2, WD, WR5);
  and and_43 (S6_2, WD, WR6);
  and and_44 (S7_2, WD, WR7);
  and and_45 (and_45_out, not_18_out, and_46_out);
  and and_46 (and_46_out, and_5_out, and_6_out);
  and and_47 (and_47_out, not_19_out, and_48_out);
  and and_48 (and_48_out, and_7_out, and_8_out);
  and and_49 (and_49_out, not_20_out, and_50_out);
  and and_50 (and_50_out, and_9_out, and_10_out);
  and and_51 (and_51_out, not_21_out, and_52_out);
  and and_52 (and_52_out, and_19_out, and_20_out);
  Sign_Extension sign_extension_1 (
    .S0(and_21_out), .S1(and_22_out), .S2(and_23_out), .S3(and_24_out), .S0_2(sign_extension_1_s0_2),
    .S1_2(sign_extension_1_s1_2), .S2_2(sign_extension_1_s2_2), .S3_2(sign_extension_1_s3_2),
    .S4(sign_extension_1_s4), .S5(sign_extension_1_s5), .S6(sign_extension_1_s6), .S7(sign_extension_1_s7));
  and and_53 (and_53_out, and_25_out, WR7);
  and and_54 (and_54_out, and_25_out, WR6);
  and and_55 (and_55_out, and_25_out, WR5);
  and and_56 (and_56_out, and_25_out, WR4);
  and and_57 (and_57_out, and_25_out, WR3);
  and and_58 (and_58_out, and_25_out, WR2);
  and and_59 (and_59_out, and_25_out, WR1);
  and and_60 (and_60_out, and_25_out, WR0);
  and and_61 (and_61_out, or_2_out, WR7);
  and and_62 (and_62_out, or_2_out, WR6);
  and and_63 (and_63_out, or_2_out, WR5);
  and and_64 (and_64_out, or_2_out, WR4);
  and and_65 (and_65_out, or_2_out, WR3);
  and and_66 (and_66_out, or_2_out, WR2);
  and and_67 (and_67_out, or_2_out, WR1);
  and and_68 (and_68_out, or_2_out, WR0);
  and and_69 (and_69_out, and_27_out, S4);
  and and_70 (and_70_out, and_27_out, S5);
  and and_71 (and_71_out, and_27_out, S6);
  and and_72 (and_72_out, and_27_out, S7);
  or or_2 (or_2_out, d_ff_1_q, and_27_out);
  or or_3 (WD, d_ff_2_q, and_47_out);
  or or_4 (LD, d_ff_3_q, and_73_out);
  and and_73 (and_73_out, CK, and_51_out);
  _8_Bit_OR u_8_bit_or_1 (
    .A0(and_53_out), .B0(and_61_out), .A1(and_54_out), .B1(and_62_out), .A2(and_55_out), .B2(and_63_out),
    .A3(and_56_out), .B3(and_64_out), .A4(and_57_out), .B4(and_65_out), .A5(and_58_out), .B5(and_66_out),
    .A6(and_59_out), .B6(and_67_out), .A7(and_60_out), .B7(and_68_out), .S0(A0), .S1(A1), .S2(A2), .S3(A3),
    .S4(A4), .S5(A5), .S6(A6), .S7(A7));
  Sign_Extension sign_extension_2 (
    .S0(and_69_out), .S1(and_70_out), .S2(and_71_out), .S3(and_72_out), .S0_2(B0), .S1_2(B1), .S2_2(B2),
    .S3_2(B3), .S4(B4), .S5(B5), .S6(B6), .S7(B7));
  ALU_ADD_CONTROL alu_add_control_1 (
    .SLB(or_2_out), .ALU0(ALU_0), .ALU1(ALU_1), .ALU2(ALU2));  // open: OR, SRB, ADD, AND, JPZ, JPC
  or or_5 (A0_2, and_29_out, and_33_out);
  or or_6 (A1_2, and_30_out, and_34_out);
  or or_7 (A2_2, and_31_out, and_35_out);
  or or_8 (A3_2, and_32_out, and_36_out);
  or or_9 (WR0_2, and_11_out, sign_extension_1_s0_2);
  or or_10 (WR1_2, and_12_out, sign_extension_1_s1_2);
  or or_11 (WR2_2, and_13_out, sign_extension_1_s2_2);
  or or_12 (WR3_2, and_14_out, sign_extension_1_s3_2);
  or or_13 (WR4_2, and_15_out, sign_extension_1_s4);
  or or_14 (WR5_2, and_16_out, sign_extension_1_s5);
  or or_15 (WR6_2, and_17_out, sign_extension_1_s6);
  or or_16 (WR7_2, and_18_out, sign_extension_1_s7);

  // Notes on the sheet:
  //   ADDN
  //   STN
  //   LDN
  //   ADDI
  //   LDI
endmodule

module Sign_Extension (
  input  S0,
  input  S1,
  input  S2,
  input  S3,
  output S0_2,
  output S1_2,
  output S2_2,
  output S3_2,
  output S4,
  output S5,
  output S6,
  output S7
);


  assign S0_2 = S0;
  assign S1_2 = S1;
  assign S2_2 = S2;
  assign S3_2 = S3;
  assign S4 = S3;
  assign S5 = S3;
  assign S6 = S3;
  assign S7 = S3;
endmodule

module _8_Bit_Adder (
  input  A0,
  input  B0,
  input  A1,
  input  B1,
  input  A2,
  input  B2,
  input  A3,
  input  B3,
  input  A4,
  input  B4,
  input  A5,
  input  B5,
  input  A6,
  input  B6,
  input  A7,
  input  B7,
  output S0,
  output S1,
  output S2,
  output S3,
  output S4,
  output S5,
  output S6,
  output S7,
  output C7
);

  wire and_1_out, and_2_out, and_3_out, and_4_out, and_5_out, and_6_out, and_7_out, and_8_out, and_9_out,
       and_10_out, and_11_out, and_12_out, and_13_out, and_14_out, and_15_out, and_16_out, and_17_out,
       and_18_out, and_19_out, and_20_out, and_21_out, and_22_out, and_23_out, and_24_out, and_25_out,
       or_1_out, or_2_out, or_3_out, or_4_out, or_5_out, or_6_out, or_7_out, or_8_out, or_9_out, or_10_out,
       or_11_out, xor_2_out, xor_3_out, xor_4_out, xor_5_out, xor_6_out, xor_7_out, xor_8_out;

  xor xor_1 (S0, A0, B0);
  and and_1 (and_1_out, B0, A0);
  xor xor_2 (xor_2_out, A1, B1);
  and and_2 (and_2_out, B1, A1);
  xor xor_3 (xor_3_out, A2, B2);
  and and_3 (and_3_out, B2, A2);
  xor xor_4 (xor_4_out, A3, B3);
  and and_4 (and_4_out, B3, A3);
  xor xor_5 (xor_5_out, A4, B4);
  and and_5 (and_5_out, B4, A4);
  xor xor_6 (xor_6_out, A5, B5);
  and and_6 (and_6_out, B5, A5);
  xor xor_7 (xor_7_out, A6, B6);
  and and_7 (and_7_out, B6, A6);
  xor xor_8 (xor_8_out, A7, B7);
  and and_8 (and_8_out, B7, A7);
  and and_9 (and_9_out, xor_2_out, and_1_out);
  or or_1 (or_1_out, and_9_out, and_2_out);
  and and_10 (and_10_out, xor_3_out, xor_4_out);
  and and_11 (and_11_out, xor_4_out, and_3_out);
  or or_2 (or_2_out, and_11_out, and_4_out);
  and and_12 (and_12_out, xor_5_out, xor_6_out);
  and and_13 (and_13_out, xor_6_out, and_5_out);
  or or_3 (or_3_out, and_13_out, and_6_out);
  and and_14 (and_14_out, xor_7_out, xor_8_out);
  and and_15 (and_15_out, xor_8_out, and_7_out);
  or or_4 (or_4_out, and_15_out, and_8_out);
  and and_16 (and_16_out, xor_3_out, or_1_out);
  or or_5 (or_5_out, and_16_out, and_3_out);
  and and_17 (and_17_out, and_10_out, or_1_out);
  or or_6 (or_6_out, and_17_out, or_2_out);
  and and_18 (and_18_out, and_12_out, xor_7_out);
  and and_19 (and_19_out, xor_7_out, or_3_out);
  and and_20 (and_20_out, and_12_out, and_14_out);
  and and_21 (and_21_out, and_14_out, or_3_out);
  and and_22 (and_22_out, xor_5_out, or_6_out);
  and and_23 (and_23_out, and_12_out, or_6_out);
  and and_24 (and_24_out, and_18_out, or_6_out);
  or or_7 (or_7_out, and_19_out, and_7_out);
  and and_25 (and_25_out, and_20_out, or_6_out);
  or or_8 (or_8_out, and_21_out, or_4_out);
  or or_9 (or_9_out, and_22_out, and_5_out);
  or or_10 (or_10_out, and_23_out, or_3_out);
  or or_11 (or_11_out, and_24_out, or_7_out);
  or or_12 (C7, and_25_out, or_8_out);
  xor xor_9 (S1, and_1_out, xor_2_out);
  xor xor_10 (S2, or_1_out, xor_3_out);
  xor xor_11 (S3, or_5_out, xor_4_out);
  xor xor_12 (S4, or_6_out, xor_5_out);
  xor xor_13 (S5, or_9_out, xor_6_out);
  xor xor_14 (S6, or_10_out, xor_7_out);
  xor xor_15 (S7, or_11_out, xor_8_out);
endmodule

module ALU_ADD_LOGIC (
  input  A0,
  input  A1,
  input  A2,
  input  A3,
  input  A4,
  input  A5,
  input  A6,
  input  A7,
  input  B0,
  input  B1,
  input  B2,
  input  B3,
  input  B4,
  input  B5,
  input  B6,
  input  B7,
  input  C0,
  input  C1,
  input  C2,
  output A0_2,
  output B0_2,
  output A1_2,
  output B1_2,
  output A2_2,
  output B2_2,
  output A3_2,
  output B3_2,
  output A4_2,
  output B4_2,
  output A5_2,
  output B5_2,
  output A6_2,
  output B6_2,
  output A7_2,
  output B7_2,
  output JPZ,
  output JPC
);

  wire and_1_out, and_18_out, and_19_out, and_21_out, and_22_out, not_1_out, not_2_out, not_3_out, or_1_out;

  and and_1 (and_1_out, C0, not_1_out);
  and and_2 (A0_2, A0, or_1_out);
  and and_3 (A1_2, A1, or_1_out);
  and and_4 (A2_2, A2, or_1_out);
  and and_5 (A3_2, A3, or_1_out);
  and and_6 (A4_2, A4, or_1_out);
  and and_7 (A5_2, A5, or_1_out);
  and and_8 (A6_2, A6, or_1_out);
  and and_9 (A7_2, A7, or_1_out);
  and and_10 (B0_2, B0, or_1_out);
  and and_11 (B1_2, B1, or_1_out);
  and and_12 (B2_2, B2, or_1_out);
  and and_13 (B3_2, B3, or_1_out);
  and and_14 (B4_2, B4, or_1_out);
  and and_15 (B5_2, B5, or_1_out);
  and and_16 (B6_2, B6, or_1_out);
  and and_17 (B7_2, B7, or_1_out);
  or or_1 (or_1_out, and_19_out, and_18_out);
  and and_18 (and_18_out, C1, C2);
  and and_19 (and_19_out, and_1_out, not_2_out);
  not not_1 (not_1_out, C1);
  not not_2 (not_2_out, C2);
  and and_20 (JPZ, not_3_out, and_22_out);
  and and_21 (and_21_out, C0, C1);
  and and_22 (and_22_out, C1, C2);
  not not_3 (not_3_out, C0);
  and and_23 (JPC, and_21_out, C2);
endmodule

module JPZ_Logic (
  input  S0,
  input  S1,
  input  S2,
  input  S3,
  input  S4,
  input  S5,
  input  S6,
  input  S7,
  input  C7,
  output JPZ
);

  wire not_1_out, or_1_out, or_2_out, or_3_out, or_4_out, or_5_out, or_6_out, or_7_out, or_8_out;

  or or_1 (or_1_out, S0, S1);
  or or_2 (or_2_out, or_1_out, or_3_out);
  or or_3 (or_3_out, S2, S3);
  or or_4 (or_4_out, S4, S5);
  or or_5 (or_5_out, or_4_out, or_6_out);
  or or_6 (or_6_out, S6, S7);
  or or_7 (or_7_out, or_2_out, or_5_out);
  or or_8 (or_8_out, or_7_out, C7);
  not not_1 (not_1_out, or_8_out);
  buf and_1 (JPZ, not_1_out);  // AND_Gate
endmodule

module ALU_AND_LOGIC (
  input  A0,
  input  A1,
  input  A2,
  input  A3,
  input  A4,
  input  A5,
  input  A6,
  input  A7,
  input  B0,
  input  B1,
  input  B2,
  input  B3,
  input  B4,
  input  B5,
  input  B6,
  input  B7,
  input  C0,
  input  C1,
  input  C2,
  output A0_2,
  output B0_2,
  output A1_2,
  output B1_2,
  output A2_2,
  output B2_2,
  output A3_2,
  output B3_2,
  output A4_2,
  output B4_2,
  output A5_2,
  output B5_2,
  output A6_2,
  output B6_2,
  output A7_2,
  output B7_2
);

  wire and_17_out, and_18_out, not_1_out, not_2_out;

  and and_1 (A0_2, A0, and_17_out);
  and and_2 (A1_2, A1, and_17_out);
  and and_3 (A2_2, A2, and_17_out);
  and and_4 (A3_2, A3, and_17_out);
  and and_5 (A4_2, A4, and_17_out);
  and and_6 (A5_2, A5, and_17_out);
  and and_7 (A6_2, A6, and_17_out);
  and and_8 (A7_2, A7, and_17_out);
  and and_9 (B0_2, B0, and_17_out);
  and and_10 (B1_2, B1, and_17_out);
  and and_11 (B2_2, B2, and_17_out);
  and and_12 (B3_2, B3, and_17_out);
  and and_13 (B4_2, B4, and_17_out);
  and and_14 (B5_2, B5, and_17_out);
  and and_15 (B6_2, B6, and_17_out);
  and and_16 (B7_2, B7, and_17_out);
  and and_17 (and_17_out, and_18_out, not_1_out);
  and and_18 (and_18_out, not_2_out, C1);
  not not_1 (not_1_out, C2);
  not not_2 (not_2_out, C0);
endmodule

module _8_Bit_AND (
  input  A0,
  input  B0,
  input  A1,
  input  B1,
  input  A2,
  input  B2,
  input  A3,
  input  B3,
  input  A4,
  input  B4,
  input  A5,
  input  B5,
  input  A6,
  input  B6,
  input  A7,
  input  B7,
  output S0,
  output S1,
  output S2,
  output S3,
  output S4,
  output S5,
  output S6,
  output S7
);

  and and_1 (S0, A0, B0);
  and and_2 (S1, A1, B1);
  and and_3 (S2, A2, B2);
  and and_4 (S3, A3, B3);
  and and_5 (S4, A4, B4);
  and and_6 (S5, A5, B5);
  and and_7 (S6, A6, B6);
  and and_8 (S7, A7, B7);
endmodule

module ALU_OR_LOGIC (
  input  A0,
  input  A1,
  input  A2,
  input  A3,
  input  A4,
  input  A5,
  input  A6,
  input  A7,
  input  B0,
  input  B1,
  input  B2,
  input  B3,
  input  B4,
  input  B5,
  input  B6,
  input  B7,
  input  C0,
  input  C1,
  input  C2,
  output A0_2,
  output B0_2,
  output A1_2,
  output B1_2,
  output A2_2,
  output B2_2,
  output A3_2,
  output B3_2,
  output A4_2,
  output B4_2,
  output A5_2,
  output B5_2,
  output A6_2,
  output B6_2,
  output A7_2,
  output B7_2
);

  wire and_17_out, and_18_out, not_1_out;

  and and_1 (A0_2, A0, and_17_out);
  and and_2 (A1_2, A1, and_17_out);
  and and_3 (A2_2, A2, and_17_out);
  and and_4 (A3_2, A3, and_17_out);
  and and_5 (A4_2, A4, and_17_out);
  and and_6 (A5_2, A5, and_17_out);
  and and_7 (A6_2, A6, and_17_out);
  and and_8 (A7_2, A7, and_17_out);
  and and_9 (B0_2, B0, and_17_out);
  and and_10 (B1_2, B1, and_17_out);
  and and_11 (B2_2, B2, and_17_out);
  and and_12 (B3_2, B3, and_17_out);
  and and_13 (B4_2, B4, and_17_out);
  and and_14 (B5_2, B5, and_17_out);
  and and_15 (B6_2, B6, and_17_out);
  and and_16 (B7_2, B7, and_17_out);
  and and_17 (and_17_out, and_18_out, not_1_out);
  and and_18 (and_18_out, C0, C1);
  not not_1 (not_1_out, C2);
endmodule

module _8_Bit_OR (
  input  A0,
  input  B0,
  input  A1,
  input  B1,
  input  A2,
  input  B2,
  input  A3,
  input  B3,
  input  A4,
  input  B4,
  input  A5,
  input  B5,
  input  A6,
  input  B6,
  input  A7,
  input  B7,
  output S0,
  output S1,
  output S2,
  output S3,
  output S4,
  output S5,
  output S6,
  output S7
);

  or or_1 (S0, A0, B0);
  or or_2 (S1, A1, B1);
  or or_3 (S2, A2, B2);
  or or_4 (S3, A3, B3);
  or or_5 (S4, A4, B4);
  or or_6 (S5, A5, B5);
  or or_7 (S6, A6, B6);
  or or_8 (S7, A7, B7);
endmodule

module _8_Bit_SHIFT_LEFT (
  input  A0,
  input  A1,
  input  A2,
  input  A3,
  input  A4,
  input  A5,
  input  A6,
  input  A7,
  input  C0,
  input  C1,
  input  C2,
  output S0,
  output S1,
  output S2,
  output S3,
  output S4,
  output S5,
  output S6,
  output S7,
  output C7
);

  wire and_1_out, and_2_out, not_1_out, not_2_out, not_3_out;

  not not_1 (not_1_out, 1'b1);
  and and_1 (and_1_out, and_2_out, C2);
  and and_2 (and_2_out, not_2_out, not_3_out);
  not not_2 (not_2_out, C0);
  not not_3 (not_3_out, C1);
  and and_3 (S0, not_1_out, and_1_out);
  and and_4 (S1, A0, and_1_out);
  and and_5 (S2, A1, and_1_out);
  and and_6 (S3, A2, and_1_out);
  and and_7 (S4, A3, and_1_out);
  and and_8 (S5, A4, and_1_out);
  and and_9 (S6, A5, and_1_out);
  and and_10 (S7, A6, and_1_out);
  and and_11 (C7, A7, and_1_out);
endmodule

module _8_Bit_SHIFT_RIGHT (
  input  A0,
  input  A1,
  input  A2,
  input  A3,
  input  A4,
  input  A5,
  input  A6,
  input  A7,
  input  C0,
  input  C1,
  input  C2,
  output C7,
  output S0,
  output S1,
  output S2,
  output S3,
  output S4,
  output S5,
  output S6,
  output S7
);

  wire and_1_out, and_2_out, not_1_out;

  and and_1 (and_1_out, and_2_out, C2);
  and and_2 (and_2_out, C0, not_1_out);
  not not_1 (not_1_out, C1);
  and and_3 (C7, A0, and_1_out);
  and and_4 (S0, A1, and_1_out);
  and and_5 (S1, A2, and_1_out);
  and and_6 (S2, A3, and_1_out);
  and and_7 (S3, A4, and_1_out);
  and and_8 (S4, A5, and_1_out);
  and and_9 (S5, A6, and_1_out);
  and and_10 (S6, A7, and_1_out);

  assign S7 = S6;
endmodule

module _1_Byte_ram (
  input  AD,
  input  RD,
  input  WD,
  input  S0,
  input  S1,
  input  S2,
  input  S3,
  input  S4,
  input  S5,
  input  S6,
  input  S7,
  output S0_2,
  output S1_2,
  output S2_2,
  output S3_2,
  output S4_2,
  output S5_2,
  output S6_2,
  output S7_2
);

  wire and_1_out, and_2_out, and_3_out, and_4_out, and_5_out, and_6_out, and_7_out, and_8_out, and_9_out,
       and_10_out, d_ff_1_q, d_ff_2_q, d_ff_3_q, d_ff_4_q, d_ff_5_q, d_ff_6_q, d_ff_7_q, d_ff_8_q;

  and and_1 (and_1_out, WD, AD);
  and and_2 (and_2_out, AD, RD);
  and and_3 (and_3_out, and_1_out, S0);
  and and_4 (and_4_out, and_1_out, S1);
  and and_5 (and_5_out, and_1_out, S2);
  and and_6 (and_6_out, and_1_out, S3);
  and and_7 (and_7_out, and_1_out, S4);
  and and_8 (and_8_out, and_1_out, S5);
  and and_9 (and_9_out, and_1_out, S6);
  and and_10 (and_10_out, and_1_out, S7);
  and and_11 (S0_2, and_2_out, d_ff_1_q);
  D_Flip_Flop #(.trigger("falling")) d_ff_1 (
    .clk(and_1_out), .D(and_3_out), .Q(d_ff_1_q));  // open: Qn, preset, en, reset
  and and_12 (S1_2, and_2_out, d_ff_2_q);
  D_Flip_Flop #(.trigger("falling")) d_ff_2 (
    .clk(and_1_out), .D(and_4_out), .Q(d_ff_2_q));  // open: Qn, preset, en, reset
  and and_13 (S2_2, and_2_out, d_ff_3_q);
  D_Flip_Flop #(.trigger("falling")) d_ff_3 (
    .clk(and_1_out), .D(and_5_out), .Q(d_ff_3_q));  // open: Qn, preset, en, reset
  and and_14 (S3_2, and_2_out, d_ff_4_q);
  D_Flip_Flop #(.trigger("falling")) d_ff_4 (
    .clk(and_1_out), .D(and_6_out), .Q(d_ff_4_q));  // open: Qn, preset, en, reset
  and and_15 (S5_2, and_2_out, d_ff_6_q);
  and and_16 (S4_2, and_2_out, d_ff_5_q);
  D_Flip_Flop #(.trigger("falling")) d_ff_5 (
    .clk(and_1_out), .D(and_7_out), .Q(d_ff_5_q));  // open: Qn, preset, en, reset
  D_Flip_Flop #(.trigger("falling")) d_ff_6 (
    .clk(and_1_out), .D(and_8_out), .Q(d_ff_6_q));  // open: Qn, preset, en, reset
  and and_17 (S6_2, and_2_out, d_ff_7_q);
  D_Flip_Flop #(.trigger("falling")) d_ff_7 (
    .clk(and_1_out), .D(and_9_out), .Q(d_ff_7_q));  // open: Qn, preset, en, reset
  and and_18 (S7_2, and_2_out, d_ff_8_q);
  D_Flip_Flop #(.trigger("falling")) d_ff_8 (
    .clk(and_1_out), .D(and_10_out), .Q(d_ff_8_q));  // open: Qn, preset, en, reset
endmodule

module RAM_chip_select_LOGIC (
  input  A0,
  input  A1,
  input  A2,
  input  A3,
  output _0x00,
  output _0x01,
  output _0x02,
  output _0x03,
  output _0x04,
  output _0x05,
  output _0x06,
  output _0x07,
  output _0x08,
  output _0x09,
  output _0x0A,
  output _0x0B,
  output _0x0C,
  output _0x0D,
  output _0x0E,
  output _0x0F
);

  wire and_1_out, and_3_out, and_4_out, and_6_out, and_7_out, and_9_out, and_10_out, and_12_out, and_13_out,
       and_15_out, and_16_out, and_18_out, and_19_out, and_21_out, and_22_out, and_24_out, and_25_out,
       and_27_out, and_28_out, and_30_out, and_31_out, and_33_out, and_34_out, and_36_out, and_37_out,
       and_39_out, and_40_out, and_42_out, and_43_out, and_45_out, and_46_out, and_48_out, not_1_out,
       not_2_out, not_3_out, not_4_out, not_5_out, not_6_out, not_7_out, not_8_out, not_9_out, not_10_out,
       not_11_out, not_12_out, not_13_out, not_14_out, not_15_out, not_16_out, not_17_out, not_18_out,
       not_19_out, not_20_out, not_21_out, not_22_out, not_23_out, not_24_out, not_25_out, not_26_out,
       not_27_out, not_28_out, not_29_out, not_30_out, not_31_out, not_32_out;

  not not_1 (not_1_out, A0);
  not not_2 (not_2_out, A1);
  not not_3 (not_3_out, A2);
  not not_4 (not_4_out, A3);
  not not_5 (not_5_out, A1);
  not not_6 (not_6_out, A2);
  not not_7 (not_7_out, A3);
  not not_8 (not_8_out, A0);
  not not_9 (not_9_out, A2);
  not not_10 (not_10_out, A3);
  not not_11 (not_11_out, A2);
  not not_12 (not_12_out, A3);
  not not_13 (not_13_out, A0);
  not not_14 (not_14_out, A1);
  not not_15 (not_15_out, A3);
  not not_16 (not_16_out, A1);
  not not_17 (not_17_out, A3);
  not not_18 (not_18_out, A0);
  not not_19 (not_19_out, A3);
  not not_20 (not_20_out, A3);
  not not_21 (not_21_out, A0);
  not not_22 (not_22_out, A1);
  not not_23 (not_23_out, A2);
  not not_24 (not_24_out, A1);
  not not_25 (not_25_out, A2);
  not not_26 (not_26_out, A0);
  not not_27 (not_27_out, A2);
  not not_28 (not_28_out, A2);
  not not_29 (not_29_out, A0);
  not not_30 (not_30_out, A1);
  not not_31 (not_31_out, A1);
  not not_32 (not_32_out, A0);
  and and_1 (and_1_out, not_1_out, not_2_out);
  and and_2 (_0x00, and_1_out, and_3_out);
  and and_3 (and_3_out, not_3_out, not_4_out);
  and and_4 (and_4_out, A0, not_5_out);
  and and_5 (_0x01, and_4_out, and_6_out);
  and and_6 (and_6_out, not_6_out, not_7_out);
  and and_7 (and_7_out, not_8_out, A1);
  and and_8 (_0x02, and_7_out, and_9_out);
  and and_9 (and_9_out, not_9_out, not_10_out);
  and and_10 (and_10_out, A0, A1);
  and and_11 (_0x03, and_10_out, and_12_out);
  and and_12 (and_12_out, not_11_out, not_12_out);
  and and_13 (and_13_out, not_13_out, not_14_out);
  and and_14 (_0x04, and_13_out, and_15_out);
  and and_15 (and_15_out, A2, not_15_out);
  and and_16 (and_16_out, A0, not_16_out);
  and and_17 (_0x05, and_16_out, and_18_out);
  and and_18 (and_18_out, A2, not_17_out);
  and and_19 (and_19_out, not_18_out, A1);
  and and_20 (_0x06, and_19_out, and_21_out);
  and and_21 (and_21_out, A2, not_19_out);
  and and_22 (and_22_out, A0, A1);
  and and_23 (_0x07, and_22_out, and_24_out);
  and and_24 (and_24_out, A2, not_20_out);
  and and_25 (and_25_out, not_21_out, not_22_out);
  and and_26 (_0x08, and_25_out, and_27_out);
  and and_27 (and_27_out, not_23_out, A3);
  and and_28 (and_28_out, A0, not_24_out);
  and and_29 (_0x09, and_28_out, and_30_out);
  and and_30 (and_30_out, not_25_out, A3);
  and and_31 (and_31_out, not_26_out, A1);
  and and_32 (_0x0A, and_31_out, and_33_out);
  and and_33 (and_33_out, not_27_out, A3);
  and and_34 (and_34_out, A0, A1);
  and and_35 (_0x0B, and_34_out, and_36_out);
  and and_36 (and_36_out, not_28_out, A3);
  and and_37 (and_37_out, not_29_out, not_30_out);
  and and_38 (_0x0C, and_37_out, and_39_out);
  and and_39 (and_39_out, A2, A3);
  and and_40 (and_40_out, A0, not_31_out);
  and and_41 (_0x0D, and_40_out, and_42_out);
  and and_42 (and_42_out, A2, A3);
  and and_43 (and_43_out, not_32_out, A1);
  and and_44 (_0x0E, and_43_out, and_45_out);
  and and_45 (and_45_out, A2, A3);
  and and_46 (and_46_out, A0, A1);
  and and_47 (_0x0F, and_46_out, and_48_out);
  and and_48 (and_48_out, A2, A3);
endmodule

module ALU_CONROL_OR (
  input  ALU0,
  input  ALU2,
  input  ALU4,
  input  ALU6,
  input  ALU1,
  input  ALU3,
  input  ALU5,
  input  ALU7,
  input  CTRL0,
  input  CTRL1,
  input  CTRL2,
  input  CTRL3,
  input  CTRL4,
  input  CTRL5,
  input  CTRL6,
  input  CTRL7,
  output out_17,
  output out_18,
  output out_19,
  output out_20,
  output out_21,
  output out_22,
  output out_23,
  output out_24
);

  _8_Bit_OR u_8_bit_or_1 (
    .A0(CTRL0), .B0(ALU0), .A1(CTRL1), .B1(ALU1), .A2(CTRL2), .B2(ALU2), .A3(CTRL3), .B3(ALU3), .A4(CTRL4),
    .B4(ALU4), .A5(CTRL5), .B5(ALU5), .A6(CTRL6), .B6(ALU6), .A7(CTRL7), .B7(ALU7), .S0(out_17), .S1(out_18),
    .S2(out_19), .S3(out_20), .S4(out_21), .S5(out_22), .S6(out_23), .S7(out_24));
endmodule

module JUMP_DELAY (
  input  JPC,
  input  JPZ,
  input  CK,
  input  rst,
  output JPC_2,
  output JPZ_2
);

  wire d_ff_2_q;

  D_Flip_Flop #(.trigger("falling")) d_ff_1 (.clk(CK), .D(JPC), .Q(JPC_2), .reset(d_ff_2_q));  // open: Qn, preset, en
  D_Flip_Flop #(.trigger("falling")) d_ff_2 (.clk(CK), .D(rst), .Q(d_ff_2_q));  // open: Qn, preset, en, reset
  D_Flip_Flop #(.trigger("falling")) d_ff_3 (.clk(CK), .D(JPZ), .Q(JPZ_2), .reset(d_ff_2_q));  // open: Qn, preset, en
endmodule

module BUTTON_PRESS_SPIKE_GENERATOR (
  input  CK,
  input  BTN0,
  input  BTN1,
  input  BTN1_2,
  input  BTN1_3,
  input  BTN1_4,
  input  BTN1_5,
  input  BTN1_6,
  input  BTN1_7,
  output IN0,
  output IN1,
  output IN1_2,
  output IN1_3,
  output IN1_4,
  output IN1_5,
  output IN1_6,
  output IN1_7
);

  wire and_1_out, d_ff_1_q, d_ff_2_q, d_ff_3_q, d_ff_4_q, d_ff_6_q, d_ff_8_q, d_ff_10_q, d_ff_12_q,
       d_ff_14_q, d_ff_16_q, d_ff_18_q, d_ff_20_q, d_ff_21_q, d_ff_22_q, d_ff_23_q, d_ff_24_q,
       n8_bit_adder_1_s0, n8_bit_adder_1_s1, n8_bit_adder_1_s2, n8_bit_adder_1_s3, n8_bit_adder_1_s4,
       n8_bit_adder_1_s5, n8_bit_adder_1_s6, n8_bit_adder_1_s7, not_1_out, not_2_out, not_3_out, not_4_out,
       not_5_out, not_6_out, not_7_out, not_8_out, xor_1_out, xor_2_out, xor_3_out, xor_4_out, xor_5_out,
       xor_6_out, xor_7_out, xor_8_out;

  _8_Bit_Adder u_8_bit_adder_1 (
    .A0(CK), .B0(d_ff_1_q), .A1(1'b0), .B1(d_ff_2_q), .A2(1'b0), .B2(d_ff_3_q), .A3(1'b0), .B3(d_ff_4_q),
    .A4(1'b0), .B4(d_ff_21_q), .A5(1'b0), .B5(d_ff_22_q), .A6(1'b0), .B6(d_ff_23_q), .A7(1'b0),
    .B7(d_ff_24_q), .S0(n8_bit_adder_1_s0), .S1(n8_bit_adder_1_s1), .S2(n8_bit_adder_1_s2),
    .S3(n8_bit_adder_1_s3), .S4(n8_bit_adder_1_s4), .S5(n8_bit_adder_1_s5), .S6(n8_bit_adder_1_s6),
    .S7(n8_bit_adder_1_s7));  // open: C7
  D_Flip_Flop #(.trigger("falling")) d_ff_1 (
    .clk(CK), .D(n8_bit_adder_1_s0), .Q(d_ff_1_q), .reset(and_1_out));  // open: Qn, preset, en
  and and_1 (and_1_out, n8_bit_adder_1_s2, n8_bit_adder_1_s1);
  D_Flip_Flop #(.trigger("falling")) d_ff_2 (
    .clk(CK), .D(n8_bit_adder_1_s1), .Q(d_ff_2_q), .reset(and_1_out));  // open: Qn, preset, en
  D_Flip_Flop #(.trigger("falling")) d_ff_3 (
    .clk(CK), .D(n8_bit_adder_1_s2), .Q(d_ff_3_q), .reset(and_1_out));  // open: Qn, preset, en
  D_Flip_Flop #(.trigger("falling")) d_ff_4 (
    .clk(CK), .D(n8_bit_adder_1_s3), .Q(d_ff_4_q), .reset(and_1_out));  // open: Qn, preset, en
  D_Flip_Flop d_ff_5 (.clk(n8_bit_adder_1_s2), .D(BTN0), .Q(IN0), .reset(d_ff_6_q));  // open: Qn, preset, en
  not not_1 (not_1_out, BTN0);
  D_Flip_Flop #(.trigger("high")) d_ff_6 (
    .clk(IN0), .D(xor_1_out), .Q(d_ff_6_q), .reset(not_1_out));  // open: Qn, preset, en
  xor xor_1 (xor_1_out, BTN0, n8_bit_adder_1_s2);
  D_Flip_Flop d_ff_7 (.clk(n8_bit_adder_1_s2), .D(BTN1), .Q(IN1), .reset(d_ff_8_q));  // open: Qn, preset, en
  not not_2 (not_2_out, BTN1);
  D_Flip_Flop #(.trigger("high")) d_ff_8 (
    .clk(IN1), .D(xor_2_out), .Q(d_ff_8_q), .reset(not_2_out));  // open: Qn, preset, en
  xor xor_2 (xor_2_out, BTN1, n8_bit_adder_1_s2);
  D_Flip_Flop d_ff_9 (.clk(n8_bit_adder_1_s2), .D(BTN1_2), .Q(IN1_2), .reset(d_ff_10_q));  // open: Qn, preset, en
  not not_3 (not_3_out, BTN1_2);
  D_Flip_Flop #(.trigger("high")) d_ff_10 (
    .clk(IN1_2), .D(xor_3_out), .Q(d_ff_10_q), .reset(not_3_out));  // open: Qn, preset, en
  xor xor_3 (xor_3_out, BTN1_2, n8_bit_adder_1_s2);
  D_Flip_Flop d_ff_11 (.clk(n8_bit_adder_1_s2), .D(BTN1_3), .Q(IN1_3), .reset(d_ff_12_q));  // open: Qn, preset, en
  not not_4 (not_4_out, BTN1_3);
  D_Flip_Flop #(.trigger("high")) d_ff_12 (
    .clk(IN1_3), .D(xor_4_out), .Q(d_ff_12_q), .reset(not_4_out));  // open: Qn, preset, en
  xor xor_4 (xor_4_out, BTN1_3, n8_bit_adder_1_s2);
  D_Flip_Flop d_ff_13 (.clk(n8_bit_adder_1_s2), .D(BTN1_4), .Q(IN1_4), .reset(d_ff_14_q));  // open: Qn, preset, en
  not not_5 (not_5_out, BTN1_4);
  D_Flip_Flop #(.trigger("high")) d_ff_14 (
    .clk(IN1_4), .D(xor_5_out), .Q(d_ff_14_q), .reset(not_5_out));  // open: Qn, preset, en
  xor xor_5 (xor_5_out, BTN1_4, n8_bit_adder_1_s2);
  D_Flip_Flop d_ff_15 (.clk(n8_bit_adder_1_s2), .D(BTN1_5), .Q(IN1_5), .reset(d_ff_16_q));  // open: Qn, preset, en
  not not_6 (not_6_out, BTN1_5);
  D_Flip_Flop #(.trigger("high")) d_ff_16 (
    .clk(IN1_5), .D(xor_6_out), .Q(d_ff_16_q), .reset(not_6_out));  // open: Qn, preset, en
  xor xor_6 (xor_6_out, BTN1_5, n8_bit_adder_1_s2);
  D_Flip_Flop d_ff_17 (.clk(n8_bit_adder_1_s2), .D(BTN1_6), .Q(IN1_6), .reset(d_ff_18_q));  // open: Qn, preset, en
  not not_7 (not_7_out, BTN1_6);
  D_Flip_Flop #(.trigger("high")) d_ff_18 (
    .clk(IN1_6), .D(xor_7_out), .Q(d_ff_18_q), .reset(not_7_out));  // open: Qn, preset, en
  xor xor_7 (xor_7_out, BTN1_6, n8_bit_adder_1_s2);
  D_Flip_Flop d_ff_19 (.clk(n8_bit_adder_1_s2), .D(BTN1_7), .Q(IN1_7), .reset(d_ff_20_q));  // open: Qn, preset, en
  not not_8 (not_8_out, BTN1_7);
  D_Flip_Flop #(.trigger("high")) d_ff_20 (
    .clk(IN1_7), .D(xor_8_out), .Q(d_ff_20_q), .reset(not_8_out));  // open: Qn, preset, en
  xor xor_8 (xor_8_out, BTN1_7, n8_bit_adder_1_s2);
  D_Flip_Flop #(.trigger("falling")) d_ff_21 (
    .clk(CK), .D(n8_bit_adder_1_s4), .Q(d_ff_21_q));  // open: Qn, preset, en, reset
  D_Flip_Flop #(.trigger("falling")) d_ff_22 (
    .clk(CK), .D(n8_bit_adder_1_s5), .Q(d_ff_22_q));  // open: Qn, preset, en, reset
  D_Flip_Flop #(.trigger("falling")) d_ff_23 (
    .clk(CK), .D(n8_bit_adder_1_s6), .Q(d_ff_23_q));  // open: Qn, preset, en, reset
  D_Flip_Flop #(.trigger("falling")) d_ff_24 (
    .clk(CK), .D(n8_bit_adder_1_s7), .Q(d_ff_24_q));  // open: Qn, preset, en, reset
endmodule
module Processor (
  input  ROM0,
  input  ROM1,
  input  ROM2,
  input  ROM3,
  input  ROM4,
  input  ROM5,
  input  ROM6,
  input  ROM7,
  input  CK,
  input  I0,
  input  I1,
  input  I2,
  input  I3,
  input  I4,
  input  I5,
  input  I6,
  input  I7,
  output [7:0] out_18,
  output O0,
  output O1,
  output O2,
  output O3,
  output O4,
  output O5,
  output O6,
  output O7
);

  wire alu_1_jpc, alu_1_jpz, alu_1_s0, alu_1_s1, alu_1_s2, alu_1_s3, alu_1_s4, alu_1_s5, alu_1_s6, alu_1_s7,
       alu_conrol_or_1_out_17, alu_conrol_or_1_out_18, alu_conrol_or_1_out_19, alu_conrol_or_1_out_20,
       alu_conrol_or_1_out_21, alu_conrol_or_1_out_22, alu_conrol_or_1_out_23, alu_conrol_or_1_out_24,
       control_1_a0, control_1_a0_2, control_1_a1, control_1_a1_2, control_1_a2, control_1_a2_2,
       control_1_a3, control_1_a3_2, control_1_a4, control_1_a5, control_1_a6, control_1_a7, control_1_alu0,
       control_1_alu2, control_1_alu_1, control_1_alua0, control_1_alua1, control_1_alua2, control_1_alua3,
       control_1_alua4, control_1_alua5, control_1_alua6, control_1_alua7, control_1_alub0, control_1_alub1,
       control_1_alub2, control_1_alub3, control_1_alub4, control_1_alub5, control_1_alub6, control_1_alub7,
       control_1_jpc_2, control_1_jpz_2, control_1_ld, control_1_ram0, control_1_ram1, control_1_ram2,
       control_1_ram3, control_1_ram4, control_1_ram5, control_1_ram6, control_1_ram7, control_1_rd,
       control_1_wd, control_1_wr0_2, control_1_wr1_2, control_1_wr2_2, control_1_wr3_2, control_1_wr4_2,
       control_1_wr5_2, control_1_wr6_2, control_1_wr7_2, jump_delay_1_jpc_2, jump_delay_1_jpz_2,
       jump_delay_2_jpc_2, jump_delay_2_jpz_2, or_1_out, ram_1_s0_2, ram_1_s1_2, ram_1_s2_2, ram_1_s3_2,
       ram_1_s4_2, ram_1_s5_2, ram_1_s6_2, ram_1_s7_2, working_register_1_x0_2, working_register_1_x1_2,
       working_register_1_x2_2, working_register_1_x3_2, working_register_1_x4_2, working_register_1_x5_2,
       working_register_1_x6_2, working_register_1_x7_2;

  Program_counter program_counter_1 (
    .out_11(out_18), .CK(CK), .JP(or_1_out), .A0(control_1_a0_2), .A1(control_1_a1_2), .A2(control_1_a2_2),
    .A3(control_1_a3_2), .A4(control_1_a4), .A5(control_1_a5), .A6(control_1_a6), .A7(control_1_a7));
  or or_1 (or_1_out, control_1_jpz_2, control_1_jpc_2);
  CONTROL control_1 (
    .S0(ROM0), .S1(ROM1), .S2(ROM2), .S3(ROM3), .S4(ROM4), .S5(ROM5), .S6(ROM6), .S7(ROM7), .CK(CK),
    .WR0(working_register_1_x0_2), .WR1(working_register_1_x1_2), .WR2(working_register_1_x2_2),
    .WR3(working_register_1_x3_2), .WR4(working_register_1_x4_2), .WR5(working_register_1_x5_2),
    .WR6(working_register_1_x6_2), .WR7(working_register_1_x7_2), .MEM0(ram_1_s0_2), .MEM1(ram_1_s1_2),
    .MEM2(ram_1_s2_2), .MEM3(ram_1_s3_2), .MEM4(ram_1_s4_2), .MEM5(ram_1_s5_2), .MEM6(ram_1_s6_2),
    .MEM7(ram_1_s7_2), .JPZ_2(control_1_jpz_2), .JPC_2(control_1_jpc_2), .A0_2(control_1_a0_2),
    .A1_2(control_1_a1_2), .A2_2(control_1_a2_2), .A3_2(control_1_a3_2), .A4(control_1_a4),
    .A5(control_1_a5), .A6(control_1_a6), .A7(control_1_a7), .JPZ(jump_delay_2_jpz_2),
    .JPC(jump_delay_2_jpc_2), .ALU0(control_1_alu0), .ALU_1(control_1_alu_1), .ALU2(control_1_alu2),
    .WR0_2(control_1_wr0_2), .WR1_2(control_1_wr1_2), .WR2_2(control_1_wr2_2), .WR3_2(control_1_wr3_2),
    .WR4_2(control_1_wr4_2), .WR5_2(control_1_wr5_2), .WR6_2(control_1_wr6_2), .WR7_2(control_1_wr7_2),
    .LD(control_1_ld), .A0(control_1_a0), .A1(control_1_a1), .A2(control_1_a2), .A3(control_1_a3),
    .RD(control_1_rd), .WD(control_1_wd), .RAM0(control_1_ram0), .RAM1(control_1_ram1),
    .RAM2(control_1_ram2), .RAM3(control_1_ram3), .RAM4(control_1_ram4), .RAM5(control_1_ram5),
    .RAM6(control_1_ram6), .RAM7(control_1_ram7), .ALUA0(control_1_alua0), .ALUA1(control_1_alua1),
    .ALUA2(control_1_alua2), .ALUA3(control_1_alua3), .ALUA4(control_1_alua4), .ALUA5(control_1_alua5),
    .ALUA6(control_1_alua6), .ALUA7(control_1_alua7), .ALUB0(control_1_alub0), .ALUB1(control_1_alub1),
    .ALUB2(control_1_alub2), .ALUB3(control_1_alub3), .ALUB4(control_1_alub4), .ALUB5(control_1_alub5),
    .ALUB6(control_1_alub6), .ALUB7(control_1_alub7));
  ALU alu_1 (
    .A0(control_1_alua0), .A1(control_1_alua1), .A2(control_1_alua2), .A3(control_1_alua3),
    .A4(control_1_alua4), .A5(control_1_alua5), .A6(control_1_alua6), .A7(control_1_alua7),
    .B0(control_1_alub0), .B1(control_1_alub1), .B2(control_1_alub2), .B3(control_1_alub3),
    .B4(control_1_alub4), .B5(control_1_alub5), .B6(control_1_alub6), .B7(control_1_alub7), .JPC(alu_1_jpc),
    .JPZ(alu_1_jpz), .S0(alu_1_s0), .S1(alu_1_s1), .S2(alu_1_s2), .S3(alu_1_s3), .S4(alu_1_s4),
    .S5(alu_1_s5), .S6(alu_1_s6), .S7(alu_1_s7), .C0(control_1_alu0), .C1(control_1_alu_1),
    .C2(control_1_alu2));
  ALU_CONROL_OR alu_conrol_or_1 (
    .CTRL0(control_1_wr0_2), .CTRL1(control_1_wr1_2), .CTRL2(control_1_wr2_2), .CTRL3(control_1_wr3_2),
    .CTRL4(control_1_wr4_2), .CTRL5(control_1_wr5_2), .CTRL6(control_1_wr6_2), .CTRL7(control_1_wr7_2),
    .ALU0(alu_1_s0), .ALU1(alu_1_s1), .ALU2(alu_1_s2), .ALU3(alu_1_s3), .ALU4(alu_1_s4), .ALU5(alu_1_s5),
    .ALU6(alu_1_s6), .ALU7(alu_1_s7), .out_17(alu_conrol_or_1_out_17), .out_18(alu_conrol_or_1_out_18),
    .out_19(alu_conrol_or_1_out_19), .out_20(alu_conrol_or_1_out_20), .out_21(alu_conrol_or_1_out_21),
    .out_22(alu_conrol_or_1_out_22), .out_23(alu_conrol_or_1_out_23), .out_24(alu_conrol_or_1_out_24));
  JUMP_DELAY jump_delay_1 (
    .JPC(alu_1_jpc), .JPZ(alu_1_jpz), .CK(CK), .JPC_2(jump_delay_1_jpc_2), .JPZ_2(jump_delay_1_jpz_2));  // open: rst
  Working_Register working_register_1 (
    .X0(alu_conrol_or_1_out_17), .X1(alu_conrol_or_1_out_18), .X2(alu_conrol_or_1_out_19),
    .X3(alu_conrol_or_1_out_20), .X4(alu_conrol_or_1_out_21), .X5(alu_conrol_or_1_out_22),
    .X6(alu_conrol_or_1_out_23), .X7(alu_conrol_or_1_out_24), .CK(control_1_ld),
    .X0_2(working_register_1_x0_2), .X1_2(working_register_1_x1_2), .X2_2(working_register_1_x2_2),
    .X3_2(working_register_1_x3_2), .X4_2(working_register_1_x4_2), .X5_2(working_register_1_x5_2),
    .X6_2(working_register_1_x6_2), .X7_2(working_register_1_x7_2));
  JUMP_DELAY jump_delay_2 (
    .JPC(jump_delay_1_jpc_2), .JPZ(jump_delay_1_jpz_2), .CK(CK), .JPC_2(jump_delay_2_jpc_2),
    .JPZ_2(jump_delay_2_jpz_2));  // open: rst
  RAM ram_1 (
    .A0(control_1_a0), .A1(control_1_a1), .A2(control_1_a2), .A3(control_1_a3), .RD(control_1_rd),
    .WD(control_1_wd), .S0(control_1_ram0), .S1(control_1_ram1), .S2(control_1_ram2), .S3(control_1_ram3),
    .S4(control_1_ram4), .S5(control_1_ram5), .S6(control_1_ram6), .S7(control_1_ram7), .OUT0(O0), .OUT1(O1),
    .OUT2(O2), .OUT3(O3), .OUT4(O4), .OUT5(O5), .OUT6(O6), .OUT7(O7), .IN0(I0), .IN1(I1), .IN2(I2), .IN3(I3),
    .IN4(I4), .IN5(I5), .IN6(I6), .IN7(I7), .S0_2(ram_1_s0_2), .S1_2(ram_1_s1_2), .S2_2(ram_1_s2_2),
    .S3_2(ram_1_s3_2), .S4_2(ram_1_s4_2), .S5_2(ram_1_s5_2), .S6_2(ram_1_s6_2), .S7_2(ram_1_s7_2));
endmodule

module Program_counter (
  input  CK,
  input  JP,
  input  A0,
  input  A1,
  input  A2,
  input  A3,
  input  A4,
  input  A5,
  input  A6,
  input  A7,
  output [7:0] out_11
);

  wire and_1_out, d_ff_1_q, d_ff_3_q, n8_bit_adder_1_s0, n8_bit_adder_1_s1, n8_bit_adder_1_s2,
       n8_bit_adder_1_s3, n8_bit_adder_1_s4, n8_bit_adder_1_s5, n8_bit_adder_1_s6, n8_bit_adder_1_s7,
       n8_bit_and_1_s0, n8_bit_and_1_s1, n8_bit_and_1_s2, n8_bit_and_1_s3, n8_bit_and_1_s4, n8_bit_and_1_s5,
       n8_bit_and_1_s6, n8_bit_and_1_s7, not_1_out, not_2_out, not_3_out;

  D_Flip_Flop d_ff_1 (.clk(CK), .D(JP), .Q(d_ff_1_q));  // open: Qn, preset, en, reset
  not not_1 (not_1_out, d_ff_1_q);
  and and_1 (and_1_out, not_1_out, CK);
  _8_Bit_Adder u_8_bit_adder_1 (
    .A0(CK), .B0(out_11[0]), .A1(1'b0), .B1(out_11[1]), .A2(1'b0), .B2(out_11[2]), .A3(1'b0), .B3(out_11[3]),
    .A4(1'b0), .B4(out_11[4]), .A5(1'b0), .B5(out_11[5]), .A6(1'b0), .B6(out_11[6]), .A7(1'b0),
    .B7(out_11[7]), .S0(n8_bit_adder_1_s0), .S1(n8_bit_adder_1_s1), .S2(n8_bit_adder_1_s2),
    .S3(n8_bit_adder_1_s3), .S4(n8_bit_adder_1_s4), .S5(n8_bit_adder_1_s5), .S6(n8_bit_adder_1_s6),
    .S7(n8_bit_adder_1_s7));  // open: C7
  not not_2 (not_2_out, d_ff_3_q);
  not not_3 (not_3_out, not_2_out);
  D_Flip_Flop #(.trigger("falling")) d_ff_2 (
    .clk(and_1_out), .D(n8_bit_adder_1_s0), .Q(out_11[0]), .preset(n8_bit_and_1_s0), .reset(d_ff_3_q));  // open: Qn, en
  D_Flip_Flop d_ff_3 (.clk(CK), .D(JP), .Q(d_ff_3_q), .reset(d_ff_3_q));  // open: Qn, preset, en
  _8_Bit_AND u_8_bit_and_1 (
    .A0(not_3_out), .B0(A0), .A1(not_3_out), .B1(A1), .A2(not_3_out), .B2(A2), .A3(not_3_out), .B3(A3),
    .A4(not_3_out), .B4(A4), .A5(not_3_out), .B5(A5), .A6(not_3_out), .B6(A6), .A7(not_3_out), .B7(A7),
    .S0(n8_bit_and_1_s0), .S1(n8_bit_and_1_s1), .S2(n8_bit_and_1_s2), .S3(n8_bit_and_1_s3),
    .S4(n8_bit_and_1_s4), .S5(n8_bit_and_1_s5), .S6(n8_bit_and_1_s6), .S7(n8_bit_and_1_s7));
  D_Flip_Flop #(.trigger("falling")) d_ff_4 (
    .clk(and_1_out), .D(n8_bit_adder_1_s1), .Q(out_11[1]), .preset(n8_bit_and_1_s1), .reset(d_ff_3_q));  // open: Qn, en
  D_Flip_Flop #(.trigger("falling")) d_ff_5 (
    .clk(and_1_out), .D(n8_bit_adder_1_s2), .Q(out_11[2]), .preset(n8_bit_and_1_s2), .reset(d_ff_3_q));  // open: Qn, en
  D_Flip_Flop #(.trigger("falling")) d_ff_6 (
    .clk(and_1_out), .D(n8_bit_adder_1_s3), .Q(out_11[3]), .preset(n8_bit_and_1_s3), .reset(d_ff_3_q));  // open: Qn, en
  D_Flip_Flop #(.trigger("falling")) d_ff_7 (
    .clk(and_1_out), .D(n8_bit_adder_1_s4), .Q(out_11[4]), .preset(n8_bit_and_1_s4), .reset(d_ff_3_q));  // open: Qn, en
  D_Flip_Flop #(.trigger("falling")) d_ff_8 (
    .clk(and_1_out), .D(n8_bit_adder_1_s5), .Q(out_11[5]), .preset(n8_bit_and_1_s5), .reset(d_ff_3_q));  // open: Qn, en
  D_Flip_Flop #(.trigger("falling")) d_ff_9 (
    .clk(and_1_out), .D(n8_bit_adder_1_s6), .Q(out_11[6]), .preset(n8_bit_and_1_s6), .reset(d_ff_3_q));  // open: Qn, en
  D_Flip_Flop #(.trigger("falling")) d_ff_10 (
    .clk(and_1_out), .D(n8_bit_adder_1_s7), .Q(out_11[7]), .preset(n8_bit_and_1_s7), .reset(d_ff_3_q));  // open: Qn, en
endmodule
