// Logisim project Gate Circuit.circ as structural Verilog: 8 circuits, main circuit main
module main (
);

  wire _1_out, _2_out, and_1_out, and_2_out, and_3_out, and_4_out, and_5_out, and_6_out, and_7_out,
       and_8_out, and_9_out, and_10_out, and_11_out, and_12_out, and_13_out, and_14_out, and_15_out,
       Cancel_out, d_ff_1_q, d_ff_2_q, d_ff_3_q, d_ff_4_q, d_ff_5_q, d_ff_6_q, d_ff_7_q, d_ff_8_q, d_ff_9_q,
       d_ff_10_q, not_1_out, not_2_out, not_3_out, or_1_out, or_2_out, or_3_out, or_4_out, or_5_out,
       or_6_out, xor_1_out, xor_2_out, xor_3_out;

  Button _1 (.out(_1_out));
  Button _2 (.out(_2_out));
  Button Cancel (.out(Cancel_out));
  or or_1 (or_1_out, Cancel_out, _2_out);
  or or_2 (or_2_out, _1_out, or_1_out);
  not not_1 (not_1_out, Cancel_out);
  D_Flip_Flop d_ff_1 (.clk(or_2_out), .D(_1_out), .Q(d_ff_1_q));  // open: Qn, preset, en, reset
  D_Flip_Flop d_ff_2 (.clk(or_2_out), .D(_2_out), .Q(d_ff_2_q));  // open: Qn, preset, en, reset
  xor xor_1 (xor_1_out, d_ff_1_q, d_ff_3_q);
  and and_1 (and_1_out, d_ff_1_q, d_ff_3_q);
  xor xor_2 (xor_2_out, d_ff_6_q, d_ff_2_q);
  and and_2 (and_2_out, d_ff_6_q, d_ff_2_q);
  xor xor_3 (xor_3_out, and_1_out, xor_2_out);
  and and_3 (and_3_out, and_1_out, xor_2_out);
  or or_3 (or_3_out, and_3_out, and_2_out);
  and and_4 (and_4_out, xor_1_out, not_1_out);
  and and_5 (and_5_out, xor_3_out, not_1_out);
  D_Flip_Flop d_ff_3 (.clk(or_2_out), .D(and_4_out), .Q(d_ff_3_q));  // open: Qn, preset, en, reset
  D_Flip_Flop d_ff_4 (.clk(or_2_out), .D(xor_1_out), .Q(d_ff_4_q));  // open: Qn, preset, en, reset
  D_Flip_Flop d_ff_5 (.clk(or_2_out), .D(xor_3_out), .Q(d_ff_5_q));  // open: Qn, preset, en, reset
  D_Flip_Flop d_ff_6 (.clk(or_2_out), .D(and_5_out), .Q(d_ff_6_q));  // open: Qn, preset, en, reset
  and and_6 (and_6_out, d_ff_5_q, or_3_out);
  and and_7 (and_7_out, and_6_out, Cancel_out);
  and and_8 (and_8_out, d_ff_4_q, not_2_out);
  not not_2 (not_2_out, d_ff_5_q);
  not not_3 (not_3_out, d_ff_4_q);
  and and_9 (and_9_out, not_3_out, d_ff_5_q);
  and and_10 (and_10_out, d_ff_5_q, or_3_out);
  and and_11 (and_11_out, and_10_out, Cancel_out);
  and and_12 (and_12_out, d_ff_4_q, d_ff_5_q);
  and and_13 (and_13_out, and_12_out, Cancel_out);
  or or_4 (or_4_out, and_7_out, and_14_out);
  and and_14 (and_14_out, and_8_out, Cancel_out);
  and and_15 (and_15_out, and_9_out, Cancel_out);
  or or_5 (or_5_out, and_15_out, and_11_out);
  or or_6 (or_6_out, and_13_out, and_13_out);
  D_Flip_Flop #(.trigger("falling")) d_ff_7 (
    .clk(or_2_out), .D(or_3_out), .Q(d_ff_7_q));  // open: Qn, preset, en, reset
  D_Flip_Flop #(.trigger("high")) d_ff_8 (.clk(or_2_out), .D(or_4_out), .Q(d_ff_8_q));  // open: Qn, preset, en, reset
  D_Flip_Flop #(.trigger("high")) d_ff_9 (.clk(or_2_out), .D(or_5_out), .Q(d_ff_9_q));  // open: Qn, preset, en, reset
  D_Flip_Flop #(.trigger("high")) d_ff_10 (.clk(or_2_out), .D(or_6_out), .Q(d_ff_10_q));  // open: Qn, preset, en, reset
  LED Open (.in(d_ff_7_q));
  LED Return__1 (.in(d_ff_8_q));
  LED Return__2 (.in(d_ff_9_q));
  LED Return__3 (.in(d_ff_10_q));

  // Notes on the sheet:
  //   Had to add wasted or in order to raise the depth
  //   of the output logic to being 1 higher than that of the clock
  //   in order to get the output buffer to work
endmodule

module Half_Adder (
  input  X,
  input  Y,
  output S,
  output C
);

  xor xor_1 (S, X, Y);
  and and_1 (C, X, Y);
endmodule

module _2_Bit_Adder (
  input  in_1,
  input  in_2,
  input  in_3,
  input  in_4,
  output out_5,
  output out_6,
  output out_7
);

  wire and_1_out, half_adder_1_c, half_adder_2_c, half_adder_2_s;

  Half_Adder half_adder_1 (.X(in_1), .Y(in_2), .S(out_5), .C(half_adder_1_c));
  and and_1 (and_1_out, half_adder_1_c, half_adder_2_s);
  Half_Adder half_adder_2 (.X(in_3), .Y(in_4), .S(half_adder_2_s), .C(half_adder_2_c));
  xor xor_1 (out_6, half_adder_1_c, half_adder_2_s);
  or or_1 (out_7, and_1_out, half_adder_2_c);
endmodule

module _2_Bit_Adder___Memory___Reset (
  input  D0,
  input  D1,
  input  CK,
  input  rst,
  output S0,
  output S1,
  output C1,
  output ck_2
);

  wire and_1_out, and_2_out, d_ff_1_q, d_ff_2_q, d_ff_3_q, d_ff_4_q, not_1_out;

  D_Flip_Flop d_ff_1 (.clk(CK), .D(D0), .Q(d_ff_1_q));  // open: Qn, preset, en, reset
  D_Flip_Flop d_ff_2 (.clk(CK), .D(D1), .Q(d_ff_2_q));  // open: Qn, preset, en, reset
  not not_1 (not_1_out, rst);
  _2_Bit_Adder u_2_bit_adder_1 (
    .in_1(d_ff_1_q), .in_2(d_ff_3_q), .in_3(d_ff_2_q), .in_4(d_ff_4_q), .out_5(S0), .out_6(S1), .out_7(C1));
  and and_1 (and_1_out, S1, not_1_out);
  and and_2 (and_2_out, S0, not_1_out);
  D_Flip_Flop d_ff_3 (.clk(CK), .D(and_2_out), .Q(d_ff_3_q));  // open: Qn, preset, en, reset
  D_Flip_Flop d_ff_4 (.clk(CK), .D(and_1_out), .Q(d_ff_4_q));  // open: Qn, preset, en, reset

  assign ck_2 = CK;
endmodule

module Output_Buffer (
  input  _1,
  input  _2,
  input  _4,
  input  CK,
  output out_5,
  output out_6,
  output out_7
);

  D_Flip_Flop d_ff_1 (.clk(CK), .D(_1), .Q(out_5));  // open: Qn, preset, en, reset
  D_Flip_Flop d_ff_2 (.clk(CK), .D(_2), .Q(out_6));  // open: Qn, preset, en, reset

  assign out_7 = _4;
endmodule

module Output_Decoder (
  input  _1,
  input  _2,
  input  _4,
  input  Cancel,
  output Open,
  output Return1,
  output Return2,
  output Return3
);

  wire and_1_out, and_2_out, and_3_out, and_4_out, and_5_out, and_6_out, and_7_out, and_8_out, and_9_out,
       not_1_out, not_2_out;

  and and_1 (and_1_out, _2, _4);
  and and_2 (and_2_out, _1, not_1_out);
  not not_1 (not_1_out, _2);
  not not_2 (not_2_out, _1);
  and and_3 (and_3_out, not_2_out, _2);
  and and_4 (and_4_out, _2, _4);
  and and_5 (and_5_out, _1, _2);
  and and_6 (and_6_out, and_1_out, Cancel);
  and and_7 (and_7_out, and_2_out, Cancel);
  and and_8 (and_8_out, and_3_out, Cancel);
  and and_9 (and_9_out, and_4_out, Cancel);
  and and_10 (Return3, and_5_out, Cancel);
  or or_1 (Return1, and_6_out, and_7_out);
  or or_2 (Return2, and_8_out, and_9_out);

  assign Open = _4;
endmodule

module Full_Project (
);

  wire _1_out, _2_out, Cancel_out, display_buffer_1_out_6, display_buffer_1_out_7, display_buffer_1_out_8,
       display_buffer_1_out_9, n2_bit_adder_memory_reset_1_c1, n2_bit_adder_memory_reset_1_ck_2,
       n2_bit_adder_memory_reset_1_s0, n2_bit_adder_memory_reset_1_s1, or_1_out, or_2_out,
       output_buffer_1_out_5, output_buffer_1_out_6, output_buffer_1_out_7, output_decoder_1_open,
       output_decoder_1_return1, output_decoder_1_return2, output_decoder_1_return3;

  Button _1 (.out(_1_out));
  Button _2 (.out(_2_out));
  Button Cancel (.out(Cancel_out));
  or or_1 (or_1_out, Cancel_out, _2_out);
  _2_Bit_Adder___Memory___Reset u_2_bit_adder_memory_reset_1 (
    .D0(_1_out), .D1(_2_out), .CK(or_2_out), .rst(Cancel_out), .S0(n2_bit_adder_memory_reset_1_s0),
    .S1(n2_bit_adder_memory_reset_1_s1), .C1(n2_bit_adder_memory_reset_1_c1),
    .ck_2(n2_bit_adder_memory_reset_1_ck_2));
  or or_2 (or_2_out, _1_out, or_1_out);
  Output_Buffer output_buffer_1 (
    ._1(n2_bit_adder_memory_reset_1_s0), ._2(n2_bit_adder_memory_reset_1_s1),
    ._4(n2_bit_adder_memory_reset_1_c1), .CK(n2_bit_adder_memory_reset_1_ck_2),
    .out_5(output_buffer_1_out_5), .out_6(output_buffer_1_out_6), .out_7(output_buffer_1_out_7));
  Output_Decoder output_decoder_1 (
    ._1(output_buffer_1_out_5), ._2(output_buffer_1_out_6), ._4(output_buffer_1_out_7), .Cancel(Cancel_out),
    .Open(output_decoder_1_open), .Return1(output_decoder_1_return1), .Return2(output_decoder_1_return2),
    .Return3(output_decoder_1_return3));
  LED Open (.in(display_buffer_1_out_6));
  Display_Buffer display_buffer_1 (
    .in_1(output_decoder_1_open), .in_2(output_decoder_1_return1), .in_3(output_decoder_1_return2),
    .in_4(output_decoder_1_return3), .in_5(or_2_out), .out_6(display_buffer_1_out_6),
    .out_7(display_buffer_1_out_7), .out_8(display_buffer_1_out_8), .out_9(display_buffer_1_out_9));
  LED Return__1 (.in(display_buffer_1_out_7));
  LED Return__2 (.in(display_buffer_1_out_8));
  LED Return__3 (.in(display_buffer_1_out_9));
endmodule

module Display_Buffer (
  input  in_1,
  input  in_2,
  input  in_3,
  input  in_4,
  input  in_5,
  output out_6,
  output out_7,
  output out_8,
  output out_9
);

  D_Flip_Flop #(.trigger("falling")) d_ff_1 (.clk(in_5), .D(in_1), .Q(out_6));  // open: Qn, preset, en, reset
  D_Flip_Flop #(.trigger("falling")) d_ff_2 (.clk(in_5), .D(in_2), .Q(out_7));  // open: Qn, preset, en, reset
  D_Flip_Flop #(.trigger("falling")) d_ff_3 (.clk(in_5), .D(in_3), .Q(out_8));  // open: Qn, preset, en, reset
  D_Flip_Flop #(.trigger("falling")) d_ff_4 (.clk(in_5), .D(in_4), .Q(out_9));  // open: Qn, preset, en, reset
endmodule
